// Logisim project SYSLOG.circ as structural Verilog: 14 circuits, main circuit main
module main (
);

  wire and_1_out, boutonA_out, BoutonB_out, clock_1_out, demultiplexer_1_out0, demultiplexer_1_out1,
       demultiplexer_2_out0, demultiplexer_3_out0, DipSwitch_1_sw4, smartbutton_1_fall, smartbutton_1_long,
       smartbutton_2_fall, smartbutton_2_long;
  wire [2:0] DipSwitch_1_sw3;
  wire [3:0] decodersevnsegmnt_1_output_1, decodersevnsegmnt_1_output_8, decodersevnsegmnt_2_output_1,
       decodersevnsegmnt_2_output_8, decodersevnsegmnt_3_output_1, decodersevnsegmnt_3_output_8,
       decodersevnsegmnt_4_output_1, decodersevnsegmnt_4_output_8, decodersevnsegmnt_5_output_1,
       decodersevnsegmnt_5_output_8, decodersevnsegmnt_6_output_1, decodersevnsegmnt_6_output_8;
  wire [4:0] decalhorraire_1_hour_shift;
  wire [5:0] decalhorraire_1_hour0, decalhorraire_1_hour1, decalhorraire_1_min0, decalhorraire_1_min1,
       decalhorraire_1_sec0, decalhorraire_1_sec1, ModHorloge_1_h0, ModHorloge_1_h1, ModHorloge_1_m0,
       ModHorloge_1_m1, ModHorloge_1_s0, ModHorloge_1_s1, multiplexer_1_out, multiplexer_2_out,
       multiplexer_3_out, multiplexer_4_out, multiplexer_5_out, multiplexer_6_out;

  Clock clock_1 (.out(clock_1_out));
  Button boutonA (.out(boutonA_out));
  Button BoutonB (.out(BoutonB_out));
  LED LED_1 (.in(and_1_out));
  and and_1 (and_1_out, smartbutton_1_long, smartbutton_2_long);
  smartbutton smartbutton_1 (
    .button(boutonA_out), .clk(clock_1_out), .fall(smartbutton_1_fall), .long(smartbutton_1_long));  // open: Tlong
  smartbutton smartbutton_2 (
    .button(BoutonB_out), .clk(clock_1_out), .fall(smartbutton_2_fall), .long(smartbutton_2_long));  // open: Tlong
  Demultiplexer #(.select(3), .enable("false")) demultiplexer_1 (
    .out0(demultiplexer_1_out0), .out1(demultiplexer_1_out1), .in(smartbutton_1_fall), .sel(DipSwitch_1_sw3));  // open: out2, out3, out4, out5, out6, out7
  Demultiplexer #(.select(3), .enable("false")) demultiplexer_2 (
    .out0(demultiplexer_2_out0), .in(smartbutton_1_long), .sel(DipSwitch_1_sw3));  // open: out1, out2, out3, out4, out5, out6, out7
  Demultiplexer #(.select(3), .enable("false")) demultiplexer_3 (
    .out0(demultiplexer_3_out0), .in(smartbutton_2_fall), .sel(DipSwitch_1_sw3));  // open: out1, out2, out3, out4, out5, out6, out7
  DipSwitch #(.number(4)) DipSwitch_1 (
    .sw1(DipSwitch_1_sw3[2]), .sw2(DipSwitch_1_sw3[1]), .sw3(DipSwitch_1_sw3[0]), .sw4(DipSwitch_1_sw4));
  ModHorloge ModHorloge_1 (
    .mrst(DipSwitch_1_sw4), .clk(clock_1_out), .LongA(demultiplexer_2_out0), .ButtA(demultiplexer_1_out0),
    .ButtB(demultiplexer_3_out0), .shift(decalhorraire_1_hour_shift), .s0(ModHorloge_1_s0),
    .s1(ModHorloge_1_s1), .m0(ModHorloge_1_m0), .m1(ModHorloge_1_m1), .h0(ModHorloge_1_h0),
    .h1(ModHorloge_1_h1));
  decalhorraire decalhorraire_1 (
    .rst(DipSwitch_1_sw4), .Button(demultiplexer_1_out1), .hour1(decalhorraire_1_hour1),
    .hour0(decalhorraire_1_hour0), .min1(decalhorraire_1_min1), .min0(decalhorraire_1_min0),
    .sec1(decalhorraire_1_sec1), .sec0(decalhorraire_1_sec0), .hour_shift(decalhorraire_1_hour_shift));
  Multiplexer #(.select(3), .width(6), .enable("false")) multiplexer_1 (
    .in0(ModHorloge_1_s0), .in1(decalhorraire_1_sec0), .out(multiplexer_1_out), .sel(DipSwitch_1_sw3));  // open: in2, in3, in4, in5, in6, in7
  Multiplexer #(.select(3), .width(6), .enable("false")) multiplexer_2 (
    .in0(ModHorloge_1_s1), .in1(decalhorraire_1_sec1), .out(multiplexer_2_out), .sel(DipSwitch_1_sw3));  // open: in2, in3, in4, in5, in6, in7
  Multiplexer #(.select(3), .width(6), .enable("false")) multiplexer_3 (
    .in0(ModHorloge_1_m0), .in1(decalhorraire_1_min0), .out(multiplexer_3_out), .sel(DipSwitch_1_sw3));  // open: in2, in3, in4, in5, in6, in7
  Multiplexer #(.select(3), .width(6), .enable("false")) multiplexer_4 (
    .in0(ModHorloge_1_m1), .in1(decalhorraire_1_min1), .out(multiplexer_4_out), .sel(DipSwitch_1_sw3));  // open: in2, in3, in4, in5, in6, in7
  Multiplexer #(.select(3), .width(6), .enable("false")) multiplexer_5 (
    .in0(ModHorloge_1_h0), .in1(decalhorraire_1_hour0), .out(multiplexer_5_out), .sel(DipSwitch_1_sw3));  // open: in2, in3, in4, in5, in6, in7
  Multiplexer #(.select(3), .width(6), .enable("false")) multiplexer_6 (
    .in0(ModHorloge_1_h1), .in1(decalhorraire_1_hour1), .out(multiplexer_6_out), .sel(DipSwitch_1_sw3));  // open: in2, in3, in4, in5, in6, in7
  decodersevnsegmnt decodersevnsegmnt_1 (
    .Input_1(multiplexer_1_out[5]), .Input_2(multiplexer_1_out[4]), .Input_3(multiplexer_1_out[3]),
    .Input_4(multiplexer_1_out[2]), .Input_5(multiplexer_1_out[1]), .Input_6(multiplexer_1_out[0]),
    .Output_1(decodersevnsegmnt_1_output_1[0]), .Output_2(decodersevnsegmnt_1_output_1[1]),
    .Output_3(decodersevnsegmnt_1_output_8[1]), .Output_4(decodersevnsegmnt_1_output_8[2]),
    .Output_5(decodersevnsegmnt_1_output_8[3]), .Output_6(decodersevnsegmnt_1_output_1[2]),
    .Output_7(decodersevnsegmnt_1_output_1[3]), .Output_8(decodersevnsegmnt_1_output_8[0]));
  decodersevnsegmnt decodersevnsegmnt_3 (
    .Input_1(multiplexer_3_out[5]), .Input_2(multiplexer_3_out[4]), .Input_3(multiplexer_3_out[3]),
    .Input_4(multiplexer_3_out[2]), .Input_5(multiplexer_3_out[1]), .Input_6(multiplexer_3_out[0]),
    .Output_1(decodersevnsegmnt_3_output_1[0]), .Output_2(decodersevnsegmnt_3_output_1[1]),
    .Output_3(decodersevnsegmnt_3_output_8[1]), .Output_4(decodersevnsegmnt_3_output_8[2]),
    .Output_5(decodersevnsegmnt_3_output_8[3]), .Output_6(decodersevnsegmnt_3_output_1[2]),
    .Output_7(decodersevnsegmnt_3_output_1[3]), .Output_8(decodersevnsegmnt_3_output_8[0]));
  decodersevnsegmnt decodersevnsegmnt_5 (
    .Input_1(multiplexer_5_out[5]), .Input_2(multiplexer_5_out[4]), .Input_3(multiplexer_5_out[3]),
    .Input_4(multiplexer_5_out[2]), .Input_5(multiplexer_5_out[1]), .Input_6(multiplexer_5_out[0]),
    .Output_1(decodersevnsegmnt_5_output_1[0]), .Output_2(decodersevnsegmnt_5_output_1[1]),
    .Output_3(decodersevnsegmnt_5_output_8[1]), .Output_4(decodersevnsegmnt_5_output_8[2]),
    .Output_5(decodersevnsegmnt_5_output_8[3]), .Output_6(decodersevnsegmnt_5_output_1[2]),
    .Output_7(decodersevnsegmnt_5_output_1[3]), .Output_8(decodersevnsegmnt_5_output_8[0]));
  decodersevnsegmnt decodersevnsegmnt_2 (
    .Input_1(multiplexer_2_out[5]), .Input_2(multiplexer_2_out[4]), .Input_3(multiplexer_2_out[3]),
    .Input_4(multiplexer_2_out[2]), .Input_5(multiplexer_2_out[1]), .Input_6(multiplexer_2_out[0]),
    .Output_1(decodersevnsegmnt_2_output_1[0]), .Output_2(decodersevnsegmnt_2_output_1[1]),
    .Output_3(decodersevnsegmnt_2_output_8[1]), .Output_4(decodersevnsegmnt_2_output_8[2]),
    .Output_5(decodersevnsegmnt_2_output_8[3]), .Output_6(decodersevnsegmnt_2_output_1[2]),
    .Output_7(decodersevnsegmnt_2_output_1[3]), .Output_8(decodersevnsegmnt_2_output_8[0]));
  decodersevnsegmnt decodersevnsegmnt_4 (
    .Input_1(multiplexer_4_out[5]), .Input_2(multiplexer_4_out[4]), .Input_3(multiplexer_4_out[3]),
    .Input_4(multiplexer_4_out[2]), .Input_5(multiplexer_4_out[1]), .Input_6(multiplexer_4_out[0]),
    .Output_1(decodersevnsegmnt_4_output_1[0]), .Output_2(decodersevnsegmnt_4_output_1[1]),
    .Output_3(decodersevnsegmnt_4_output_8[1]), .Output_4(decodersevnsegmnt_4_output_8[2]),
    .Output_5(decodersevnsegmnt_4_output_8[3]), .Output_6(decodersevnsegmnt_4_output_1[2]),
    .Output_7(decodersevnsegmnt_4_output_1[3]), .Output_8(decodersevnsegmnt_4_output_8[0]));
  decodersevnsegmnt decodersevnsegmnt_6 (
    .Input_1(multiplexer_6_out[5]), .Input_2(multiplexer_6_out[4]), .Input_3(multiplexer_6_out[3]),
    .Input_4(multiplexer_6_out[2]), .Input_5(multiplexer_6_out[1]), .Input_6(multiplexer_6_out[0]),
    .Output_1(decodersevnsegmnt_6_output_1[0]), .Output_2(decodersevnsegmnt_6_output_1[1]),
    .Output_3(decodersevnsegmnt_6_output_8[1]), .Output_4(decodersevnsegmnt_6_output_8[2]),
    .Output_5(decodersevnsegmnt_6_output_8[3]), .Output_6(decodersevnsegmnt_6_output_1[2]),
    .Output_7(decodersevnsegmnt_6_output_1[3]), .Output_8(decodersevnsegmnt_6_output_8[0]));
  _7_Segment_Display L_7_Segment_Display_1 (
    .g(decodersevnsegmnt_6_output_1[3]), .f(decodersevnsegmnt_6_output_1[2]),
    .a(decodersevnsegmnt_6_output_1[0]), .b(decodersevnsegmnt_6_output_1[1]),
    .e(decodersevnsegmnt_6_output_8[3]), .d(decodersevnsegmnt_6_output_8[2]),
    .c(decodersevnsegmnt_6_output_8[1]), .dp(decodersevnsegmnt_6_output_8[0]));
  _7_Segment_Display L_7_Segment_Display_2 (
    .g(decodersevnsegmnt_5_output_1[3]), .f(decodersevnsegmnt_5_output_1[2]),
    .a(decodersevnsegmnt_5_output_1[0]), .b(decodersevnsegmnt_5_output_1[1]),
    .e(decodersevnsegmnt_5_output_8[3]), .d(decodersevnsegmnt_5_output_8[2]),
    .c(decodersevnsegmnt_5_output_8[1]), .dp(decodersevnsegmnt_5_output_8[0]));
  _7_Segment_Display L_7_Segment_Display_3 (
    .g(decodersevnsegmnt_4_output_1[3]), .f(decodersevnsegmnt_4_output_1[2]),
    .a(decodersevnsegmnt_4_output_1[0]), .b(decodersevnsegmnt_4_output_1[1]),
    .e(decodersevnsegmnt_4_output_8[3]), .d(decodersevnsegmnt_4_output_8[2]),
    .c(decodersevnsegmnt_4_output_8[1]), .dp(decodersevnsegmnt_4_output_8[0]));
  _7_Segment_Display L_7_Segment_Display_4 (
    .g(decodersevnsegmnt_3_output_1[3]), .f(decodersevnsegmnt_3_output_1[2]),
    .a(decodersevnsegmnt_3_output_1[0]), .b(decodersevnsegmnt_3_output_1[1]),
    .e(decodersevnsegmnt_3_output_8[3]), .d(decodersevnsegmnt_3_output_8[2]),
    .c(decodersevnsegmnt_3_output_8[1]), .dp(decodersevnsegmnt_3_output_8[0]));
  _7_Segment_Display L_7_Segment_Display_5 (
    .g(decodersevnsegmnt_2_output_1[3]), .f(decodersevnsegmnt_2_output_1[2]),
    .a(decodersevnsegmnt_2_output_1[0]), .b(decodersevnsegmnt_2_output_1[1]),
    .e(decodersevnsegmnt_2_output_8[3]), .d(decodersevnsegmnt_2_output_8[2]),
    .c(decodersevnsegmnt_2_output_8[1]), .dp(decodersevnsegmnt_2_output_8[0]));
  _7_Segment_Display L_7_Segment_Display_6 (
    .g(decodersevnsegmnt_1_output_1[3]), .f(decodersevnsegmnt_1_output_1[2]),
    .a(decodersevnsegmnt_1_output_1[0]), .b(decodersevnsegmnt_1_output_1[1]),
    .e(decodersevnsegmnt_1_output_8[3]), .d(decodersevnsegmnt_1_output_8[2]),
    .c(decodersevnsegmnt_1_output_8[1]), .dp(decodersevnsegmnt_1_output_8[0]));
endmodule

module Horloge (
  input  MRST,
  input  clk,
  input  longA,
  input  FallA,
  input  FallB,
  output [9:0] ms,
  output [5:0] Seconds,
  output [5:0] Minutes,
  output [4:0] Hours
);

  wire and_1_out, and_2_out, and_3_out, and_4_out, and_5_out, and_6_out, and_7_out, and_8_out, and_9_out,
       and_10_out, and_11_out, and_12_out, counter8bit_1_o0, counter8bit_1_o1, counter8bit_1_o2,
       counter8bit_1_ovrf, counter8bit_4_o0, counter8bit_4_o1, counter8bit_4_o2, counter8bit_4_o3,
       counter8bit_4_o4, counter8bit_4_o5, counter8bit_6_o0, counter8bit_6_o1, counter8bit_6_o2,
       counter8bit_6_o3, counter8bit_6_o4, d_ff_1_q, d_ff_1_qn, d_ff_2_qn, not_1_out, or_1_out, or_2_out,
       or_3_out, or_4_out, or_5_out, or_6_out;

  D_Flip_Flop d_ff_1 (.D(d_ff_1_qn), .clk(longA), .Q(d_ff_1_q), .Qn(d_ff_1_qn), .reset(MRST));  // open: preset
  D_Flip_Flop d_ff_2 (.D(d_ff_2_qn), .clk(FallA), .Qn(d_ff_2_qn), .reset(MRST));  // open: Q, preset
  and and_1 (and_1_out, counter8bit_4_o5, counter8bit_4_o4, counter8bit_4_o3, counter8bit_4_o2, ~counter8bit_4_o1, ~counter8bit_4_o0);  // AND_Gate
  and and_2 (and_2_out, counter8bit_6_o4, counter8bit_6_o3, ~counter8bit_6_o2, ~counter8bit_6_o1, ~counter8bit_6_o0);  // AND_Gate
  and and_3 (and_3_out, d_ff_2_qn, FallB);
  or or_1 (or_1_out, and_1_out, MRST);
  counter8bit counter8bit_4 (
    .EN(and_3_out), .clk(clk), .rst(or_1_out), .WRITE(1'b0), .I7(1'b0), .I6(1'b0), .I5(1'b0), .I4(1'b0),
    .I3(1'b0), .I2(1'b0), .I1(1'b0), .I0(1'b0), .O5(counter8bit_4_o5), .O4(counter8bit_4_o4),
    .O3(counter8bit_4_o3), .O2(counter8bit_4_o2), .O1(counter8bit_4_o1), .O0(counter8bit_4_o0));  // open: OVRF, O7, O6
  and and_4 (and_4_out, not_1_out, FallB);
  or or_2 (or_2_out, and_2_out, MRST);
  counter8bit counter8bit_6 (
    .EN(and_4_out), .clk(clk), .rst(or_2_out), .WRITE(1'b0), .I7(1'b0), .I6(1'b0), .I5(1'b0), .I4(1'b0),
    .I3(1'b0), .I2(1'b0), .I1(1'b0), .I0(1'b0), .O4(counter8bit_6_o4), .O3(counter8bit_6_o3),
    .O2(counter8bit_6_o2), .O1(counter8bit_6_o1), .O0(counter8bit_6_o0));  // open: OVRF, O7, O6, O5
  not not_1 (not_1_out, d_ff_2_qn);
  or or_3 (or_3_out, MRST, and_11_out);
  or or_4 (or_4_out, MRST, and_5_out);
  or or_5 (or_5_out, MRST, and_6_out);
  or or_6 (or_6_out, MRST, and_7_out);
  and and_5 (and_5_out, Seconds[5], Seconds[4], Seconds[3], Seconds[2], ~Seconds[1], ~Seconds[0]);  // AND_Gate
  and and_6 (and_6_out, Minutes[5], Minutes[4], Minutes[3], Minutes[2], ~Minutes[1], ~Minutes[0]);  // AND_Gate
  and and_7 (and_7_out, Hours[4], Hours[3], ~Hours[2], ~Hours[1], ~Hours[0]);  // AND_Gate
  counter8bit counter8bit_1 (
    .EN(1'b1), .clk(clk), .rst(or_3_out), .WRITE(1'b0), .I7(1'b0), .I6(1'b0), .I5(1'b0), .I4(1'b0),
    .I3(1'b0), .OVRF(counter8bit_1_ovrf), .O7(ms[4]), .O6(ms[3]), .O5(ms[2]), .O4(ms[1]), .O3(ms[0]),
    .O2(counter8bit_1_o2), .O1(counter8bit_1_o1), .O0(counter8bit_1_o0));  // open: I2, I1, I0
  and and_8 (and_8_out, ~counter8bit_1_o2, ~counter8bit_1_o1, ~counter8bit_1_o0);  // AND_Gate
  counter8bit counter8bit_3 (
    .EN(and_12_out), .clk(clk), .rst(or_4_out), .WRITE(1'b0), .I7(1'b0), .I6(1'b0), .I5(1'b0), .I4(1'b0),
    .I3(1'b0), .I2(1'b0), .I1(1'b0), .I0(1'b0), .O5(Seconds[5]), .O4(Seconds[4]), .O3(Seconds[3]),
    .O2(Seconds[2]), .O1(Seconds[1]), .O0(Seconds[0]));  // open: OVRF, O7, O6
  and and_9 (and_9_out, Seconds[0], Seconds[1], ~Seconds[2], Seconds[3], Seconds[4], Seconds[5]);  // AND_Gate
  counter8bit counter8bit_5 (
    .EN(and_9_out), .clk(clk), .rst(or_5_out), .WRITE(d_ff_1_q), .I7(1'b0), .I6(1'b0), .I5(counter8bit_4_o5),
    .I4(counter8bit_4_o4), .I3(counter8bit_4_o3), .I2(counter8bit_4_o2), .I1(counter8bit_4_o1),
    .I0(counter8bit_4_o0), .O5(Minutes[5]), .O4(Minutes[4]), .O3(Minutes[3]), .O2(Minutes[2]),
    .O1(Minutes[1]), .O0(Minutes[0]));  // open: OVRF, O7, O6
  and and_10 (and_10_out, Minutes[0], Minutes[1], ~Minutes[2], Minutes[3], Minutes[4], Minutes[5]);  // AND_Gate
  counter8bit counter8bit_7 (
    .EN(and_10_out), .clk(clk), .rst(or_6_out), .WRITE(d_ff_1_q), .I7(1'b0), .I6(1'b0), .I5(1'b0),
    .I4(counter8bit_6_o4), .I3(counter8bit_6_o3), .I2(counter8bit_6_o2), .I1(counter8bit_6_o1),
    .I0(counter8bit_6_o0), .O4(Hours[4]), .O3(Hours[3]), .O2(Hours[2]), .O1(Hours[1]), .O0(Hours[0]));  // open: OVRF, O7, O6, O5
  counter8bit counter8bit_2 (
    .EN(counter8bit_1_ovrf), .clk(clk), .rst(or_3_out), .WRITE(1'b0), .I4(1'b0), .I3(1'b0), .I2(1'b0),
    .I1(1'b0), .I0(1'b0), .O4(ms[9]), .O3(ms[8]), .O2(ms[7]), .O1(ms[6]), .O0(ms[5]));  // open: I7, I6, I5, OVRF, O7, O6, O5
  and and_11 (and_11_out, ms[0], ~ms[1], ~ms[2], ms[3], ~ms[4], ms[5], ms[6], ms[7], ms[8], ms[9]);  // AND_Gate
  and and_12 (and_12_out, ~ms[0], ~ms[1], ~ms[2], ms[3], ~ms[4], ms[5], ms[6], ms[7], ms[8], ms[9], and_8_out);  // AND_Gate
endmodule

module ones (
  input  Input_1,
  input  Input_2,
  input  Input_3,
  input  Input_4,
  input  Input_5,
  input  Input_6,
  output Output_1,
  output Output_2,
  output Output_3,
  output Output_4,
  output Output_5,
  output Output_6
);

  wire and_1_out, and_2_out, and_3_out, and_4_out, and_5_out, and_6_out, and_7_out, and_8_out, and_9_out,
       and_10_out, and_11_out, and_12_out, and_13_out, and_14_out, and_15_out, and_16_out, and_17_out,
       and_18_out, and_19_out, and_20_out, and_21_out, and_22_out, and_23_out, and_24_out, not_1_out,
       not_2_out, not_3_out, not_4_out, not_5_out, not_6_out, not_7_out, not_8_out, not_9_out, not_10_out,
       not_11_out, not_12_out, not_13_out, not_14_out, not_15_out, not_16_out, not_17_out, not_18_out,
       not_19_out, not_20_out, not_21_out, not_22_out, not_23_out, not_24_out, not_25_out, not_26_out,
       not_27_out, not_28_out, not_29_out, not_30_out, not_31_out, not_32_out, not_33_out, not_34_out,
       not_35_out, not_36_out, not_37_out, not_38_out, not_39_out, not_40_out, not_41_out, not_42_out,
       not_43_out, not_44_out, not_45_out, not_46_out, not_47_out, not_48_out, not_49_out, not_50_out,
       not_51_out, not_52_out, not_53_out, not_54_out;

  not not_1 (not_1_out, Input_1);
  not not_2 (not_2_out, Input_2);
  not not_3 (not_3_out, Input_4);
  not not_4 (not_4_out, Input_5);
  not not_5 (not_5_out, Input_1);
  not not_6 (not_6_out, Input_3);
  not not_7 (not_7_out, Input_4);
  not not_8 (not_8_out, Input_1);
  not not_9 (not_9_out, Input_5);
  not not_10 (not_10_out, Input_2);
  not not_11 (not_11_out, Input_3);
  not not_12 (not_12_out, Input_3);
  not not_13 (not_13_out, Input_4);
  not not_14 (not_14_out, Input_5);
  not not_15 (not_15_out, Input_4);
  not not_16 (not_16_out, Input_2);
  not not_17 (not_17_out, Input_3);
  not not_18 (not_18_out, Input_5);
  not not_19 (not_19_out, Input_1);
  not not_20 (not_20_out, Input_2);
  not not_21 (not_21_out, Input_1);
  not not_22 (not_22_out, Input_4);
  not not_23 (not_23_out, Input_5);
  not not_24 (not_24_out, Input_1);
  not not_25 (not_25_out, Input_4);
  not not_26 (not_26_out, Input_4);
  not not_27 (not_27_out, Input_5);
  not not_28 (not_28_out, Input_2);
  not not_29 (not_29_out, Input_3);
  not not_30 (not_30_out, Input_4);
  not not_31 (not_31_out, Input_2);
  not not_32 (not_32_out, Input_3);
  not not_33 (not_33_out, Input_1);
  not not_34 (not_34_out, Input_2);
  not not_35 (not_35_out, Input_3);
  not not_36 (not_36_out, Input_1);
  not not_37 (not_37_out, Input_3);
  not not_38 (not_38_out, Input_1);
  not not_39 (not_39_out, Input_2);
  not not_40 (not_40_out, Input_5);
  not not_41 (not_41_out, Input_1);
  not not_42 (not_42_out, Input_3);
  not not_43 (not_43_out, Input_4);
  not not_44 (not_44_out, Input_5);
  not not_45 (not_45_out, Input_1);
  not not_46 (not_46_out, Input_4);
  not not_47 (not_47_out, Input_2);
  not not_48 (not_48_out, Input_3);
  not not_49 (not_49_out, Input_5);
  not not_50 (not_50_out, Input_3);
  not not_51 (not_51_out, Input_5);
  not not_52 (not_52_out, Input_2);
  not not_53 (not_53_out, Input_4);
  not not_54 (not_54_out, Input_5);
  and and_1 (and_1_out, not_1_out, not_2_out, Input_3, not_3_out, not_4_out);
  and and_2 (and_2_out, not_5_out, Input_2, not_6_out, not_7_out, Input_5);
  and and_3 (and_3_out, not_8_out, Input_2, Input_3, Input_4, not_9_out);
  and and_4 (and_4_out, Input_1, not_10_out, not_11_out, Input_4, Input_5);
  and and_5 (and_5_out, Input_1, Input_2, not_12_out, not_13_out, not_14_out);
  and and_6 (and_6_out, Input_1, Input_2, Input_3, not_15_out, Input_5);
  and and_7 (and_7_out, not_16_out, not_17_out, Input_4, not_18_out);
  and and_8 (and_8_out, not_19_out, not_20_out, Input_4, Input_5);
  and and_9 (and_9_out, not_21_out, Input_2, not_22_out, not_23_out);
  and and_10 (and_10_out, not_24_out, Input_2, Input_3, not_25_out);
  and and_11 (and_11_out, Input_2, Input_3, not_26_out, not_27_out);
  and and_12 (and_12_out, Input_1, not_28_out, not_29_out, not_30_out, Input_5);
  and and_13 (and_13_out, Input_1, not_31_out, Input_3, Input_4);
  and and_14 (and_14_out, Input_1, Input_2, not_32_out, Input_4, Input_5);
  and and_15 (and_15_out, not_33_out, not_34_out, not_35_out, Input_5);
  and and_16 (and_16_out, not_36_out, not_37_out, Input_4, Input_5);
  and and_17 (and_17_out, not_38_out, not_39_out, Input_3, Input_4, not_40_out);
  and and_18 (and_18_out, not_41_out, Input_2, not_42_out, not_43_out, not_44_out);
  and and_19 (and_19_out, not_45_out, Input_2, Input_3, not_46_out, Input_5);
  and and_20 (and_20_out, Input_1, not_47_out, not_48_out, not_49_out);
  and and_21 (and_21_out, Input_1, not_50_out, Input_4, not_51_out);
  and and_22 (and_22_out, Input_1, not_52_out, Input_3, Input_5);
  and and_23 (and_23_out, Input_1, Input_3, Input_4, Input_5);
  and and_24 (and_24_out, Input_1, Input_2, Input_3, not_53_out, not_54_out);
  or or_1 (Output_3, and_1_out, and_2_out, and_3_out, and_4_out, and_5_out, and_6_out);
  or or_2 (Output_4, and_7_out, and_8_out, and_9_out, and_10_out, and_11_out, and_12_out, and_13_out, and_14_out);
  or or_3 (Output_5, and_15_out, and_16_out, and_17_out, and_18_out, and_19_out, and_20_out, and_21_out, and_22_out, and_23_out, and_24_out);

  assign Output_1 = 1'b0;
  assign Output_2 = 1'b0;
  assign Output_6 = Input_6;
endmodule

module tens (
  input  Input_1,
  input  Input_2,
  input  Input_3,
  input  Input_4,
  input  Input_5,
  input  Input_6,
  output Output_1,
  output Output_2,
  output Output_3,
  output Output_4,
  output Output_5,
  output Output_6
);

  wire and_1_out, and_2_out, and_3_out, and_4_out, and_5_out, and_6_out, and_7_out, and_8_out, and_9_out,
       and_10_out, and_11_out, and_12_out, and_13_out, and_14_out, not_1_out, not_2_out, not_3_out,
       not_4_out, not_5_out, not_6_out, not_7_out, not_8_out, not_9_out, not_10_out, not_11_out, not_12_out,
       not_13_out, not_14_out, not_15_out, not_16_out, not_17_out;

  and and_1 (and_1_out, Input_1, Input_3);
  and and_2 (and_2_out, Input_1, Input_2);
  not not_1 (not_1_out, Input_1);
  and and_3 (and_3_out, not_1_out, Input_2, Input_4);
  not not_2 (not_2_out, Input_1);
  and and_4 (and_4_out, not_2_out, Input_2, Input_3);
  and and_5 (and_5_out, Input_2, Input_3, Input_4);
  not not_3 (not_3_out, Input_2);
  and and_6 (and_6_out, Input_1, not_3_out, not_4_out);
  not not_4 (not_4_out, Input_3);
  not not_5 (not_5_out, Input_1);
  not not_6 (not_6_out, Input_2);
  not not_7 (not_7_out, Input_1);
  not not_8 (not_8_out, Input_2);
  not not_9 (not_9_out, Input_1);
  not not_10 (not_10_out, Input_1);
  not not_11 (not_11_out, Input_3);
  not not_12 (not_12_out, Input_4);
  not not_13 (not_13_out, Input_2);
  not not_14 (not_14_out, Input_3);
  not not_15 (not_15_out, Input_3);
  not not_16 (not_16_out, Input_3);
  not not_17 (not_17_out, Input_4);
  or or_1 (Output_4, and_1_out, and_2_out);
  or or_2 (Output_5, and_3_out, and_4_out, and_5_out, and_6_out);
  and and_7 (and_7_out, not_5_out, not_6_out, Input_3, Input_5);
  and and_8 (and_8_out, not_7_out, not_8_out, Input_3, Input_4);
  and and_9 (and_9_out, not_9_out, Input_3, Input_4, Input_5);
  and and_10 (and_10_out, not_10_out, Input_2, not_11_out, not_12_out);
  and and_11 (and_11_out, Input_1, not_13_out, not_14_out);
  and and_12 (and_12_out, Input_1, not_15_out, Input_5);
  and and_13 (and_13_out, Input_1, not_16_out, Input_4);
  and and_14 (and_14_out, Input_1, Input_2, Input_3, not_17_out);
  or or_3 (Output_6, and_7_out, and_8_out, and_9_out, and_10_out, and_11_out, and_12_out, and_13_out, and_14_out);

  assign Output_1 = 1'b0;
  assign Output_2 = 1'b0;
  assign Output_3 = 1'b0;
endmodule

module decodersevnsegmnt (
  input  Input_1,
  input  Input_2,
  input  Input_3,
  input  Input_4,
  input  Input_5,
  input  Input_6,
  output Output_1,
  output Output_2,
  output Output_3,
  output Output_4,
  output Output_5,
  output Output_6,
  output Output_7,
  output Output_8
);

  wire and_1_out, and_2_out, and_3_out, and_4_out, and_5_out, and_6_out, and_7_out, and_8_out, and_9_out,
       and_10_out, and_11_out, and_12_out, and_13_out, and_14_out, and_15_out, and_16_out, and_17_out,
       and_18_out, and_19_out, and_20_out, and_21_out, and_22_out, and_23_out, and_24_out, and_25_out,
       and_26_out, and_27_out, and_28_out, and_29_out, and_30_out, and_31_out, and_32_out, and_33_out,
       and_34_out, and_35_out, and_36_out, and_37_out, and_38_out, and_39_out, and_40_out, and_41_out,
       and_42_out, and_43_out, and_44_out, and_45_out, and_46_out, and_47_out, and_48_out, and_49_out,
       and_50_out, and_51_out, and_52_out, and_53_out, and_54_out, and_55_out, and_56_out, and_57_out,
       and_58_out, and_59_out, and_60_out, and_61_out, and_62_out, and_63_out, and_64_out, and_65_out,
       and_66_out, and_67_out, and_68_out, and_69_out, and_70_out, and_71_out, and_72_out, and_73_out,
       and_74_out, and_75_out, and_76_out, and_77_out, and_78_out, and_79_out, and_80_out, and_81_out,
       and_82_out, and_83_out, and_84_out, not_1_out, not_2_out, not_3_out, not_4_out, not_5_out, not_6_out,
       not_7_out, not_8_out, not_9_out, not_10_out, not_11_out, not_12_out, not_13_out, not_14_out,
       not_15_out, not_16_out, not_17_out, not_18_out, not_19_out, not_20_out, not_21_out, not_22_out,
       not_23_out, not_24_out, not_25_out, not_26_out, not_27_out, not_28_out, not_29_out, not_30_out,
       not_31_out, not_32_out, not_33_out, not_34_out, not_35_out, not_36_out, not_37_out, not_38_out,
       not_39_out, not_40_out, not_41_out, not_42_out, not_43_out, not_44_out, not_45_out, not_46_out,
       not_47_out, not_48_out, not_49_out, not_50_out, not_51_out, not_52_out, not_53_out, not_54_out,
       not_55_out, not_56_out, not_57_out, not_58_out, not_59_out, not_60_out, not_61_out, not_62_out,
       not_63_out, not_64_out, not_65_out, not_66_out, not_67_out, not_68_out, not_69_out, not_70_out,
       not_71_out, not_72_out, not_73_out, not_74_out, not_75_out, not_76_out, not_77_out, not_78_out,
       not_79_out, not_80_out, not_81_out, not_82_out, not_83_out, not_84_out, not_85_out, not_86_out,
       not_87_out, not_88_out, not_89_out, not_90_out, not_91_out, not_92_out, not_93_out, not_94_out,
       not_95_out, not_96_out, not_97_out, not_98_out, not_99_out, not_100_out, not_101_out, not_102_out,
       not_103_out, not_104_out, not_105_out, not_106_out, not_107_out, not_108_out, not_109_out,
       not_110_out, not_111_out, not_112_out, not_113_out, not_114_out, not_115_out, not_116_out,
       not_117_out, not_118_out, not_119_out, not_120_out, not_121_out, not_122_out, not_123_out,
       not_124_out, not_125_out, not_126_out, not_127_out, not_128_out, not_129_out, not_130_out,
       not_131_out, not_132_out, not_133_out, not_134_out, not_135_out, not_136_out, not_137_out,
       not_138_out, not_139_out, not_140_out, not_141_out, not_142_out, not_143_out, not_144_out,
       not_145_out, not_146_out, not_147_out, not_148_out, not_149_out, not_150_out, not_151_out,
       not_152_out, not_153_out, not_154_out, not_155_out, not_156_out, not_157_out, not_158_out,
       not_159_out, not_160_out, not_161_out, not_162_out, not_163_out, not_164_out, not_165_out,
       not_166_out, not_167_out, not_168_out, not_169_out, not_170_out, not_171_out, not_172_out,
       not_173_out, not_174_out, not_175_out, not_176_out, not_177_out, not_178_out, not_179_out,
       not_180_out, not_181_out, not_182_out, not_183_out, not_184_out, not_185_out, not_186_out,
       not_187_out, not_188_out, not_189_out, not_190_out, not_191_out, not_192_out, not_193_out,
       not_194_out, not_195_out, not_196_out, not_197_out, not_198_out, not_199_out, not_200_out,
       not_201_out, not_202_out, not_203_out, not_204_out, not_205_out, not_206_out, not_207_out,
       not_208_out, not_209_out, not_210_out, not_211_out, not_212_out, not_213_out, not_214_out,
       not_215_out, not_216_out, not_217_out, not_218_out, not_219_out, not_220_out, not_221_out;

  not not_1 (not_1_out, Input_1);
  not not_2 (not_2_out, Input_2);
  not not_3 (not_3_out, Input_4);
  not not_4 (not_4_out, Input_5);
  not not_5 (not_5_out, Input_6);
  not not_6 (not_6_out, Input_1);
  not not_7 (not_7_out, Input_2);
  not not_8 (not_8_out, Input_3);
  not not_9 (not_9_out, Input_1);
  not not_10 (not_10_out, Input_3);
  not not_11 (not_11_out, Input_1);
  not not_12 (not_12_out, Input_5);
  not not_13 (not_13_out, Input_1);
  not not_14 (not_14_out, Input_2);
  not not_15 (not_15_out, Input_2);
  not not_16 (not_16_out, Input_5);
  not not_17 (not_17_out, Input_1);
  not not_18 (not_18_out, Input_3);
  not not_19 (not_19_out, Input_4);
  not not_20 (not_20_out, Input_5);
  not not_21 (not_21_out, Input_3);
  not not_22 (not_22_out, Input_4);
  not not_23 (not_23_out, Input_5);
  not not_24 (not_24_out, Input_6);
  not not_25 (not_25_out, Input_1);
  not not_26 (not_26_out, Input_4);
  not not_27 (not_27_out, Input_2);
  not not_28 (not_28_out, Input_4);
  not not_29 (not_29_out, Input_6);
  not not_30 (not_30_out, Input_2);
  not not_31 (not_31_out, Input_4);
  not not_32 (not_32_out, Input_5);
  not not_33 (not_33_out, Input_1);
  not not_34 (not_34_out, Input_2);
  not not_35 (not_35_out, Input_4);
  not not_36 (not_36_out, Input_2);
  not not_37 (not_37_out, Input_3);
  not not_38 (not_38_out, Input_4);
  not not_39 (not_39_out, Input_1);
  not not_40 (not_40_out, Input_3);
  not not_41 (not_41_out, Input_4);
  not not_42 (not_42_out, Input_6);
  not not_43 (not_43_out, Input_1);
  not not_44 (not_44_out, Input_3);
  not not_45 (not_45_out, Input_5);
  not not_46 (not_46_out, Input_6);
  not not_47 (not_47_out, Input_1);
  not not_48 (not_48_out, Input_2);
  not not_49 (not_49_out, Input_6);
  not not_50 (not_50_out, Input_1);
  not not_51 (not_51_out, Input_3);
  not not_52 (not_52_out, Input_1);
  not not_53 (not_53_out, Input_4);
  not not_54 (not_54_out, Input_3);
  not not_55 (not_55_out, Input_4);
  not not_56 (not_56_out, Input_5);
  not not_57 (not_57_out, Input_2);
  not not_58 (not_58_out, Input_4);
  not not_59 (not_59_out, Input_6);
  not not_60 (not_60_out, Input_2);
  not not_61 (not_61_out, Input_1);
  not not_62 (not_62_out, Input_2);
  not not_63 (not_63_out, Input_5);
  not not_64 (not_64_out, Input_6);
  not not_65 (not_65_out, Input_2);
  not not_66 (not_66_out, Input_3);
  not not_67 (not_67_out, Input_4);
  not not_68 (not_68_out, Input_5);
  not not_69 (not_69_out, Input_1);
  not not_70 (not_70_out, Input_2);
  not not_71 (not_71_out, Input_3);
  not not_72 (not_72_out, Input_1);
  not not_73 (not_73_out, Input_3);
  not not_74 (not_74_out, Input_5);
  not not_75 (not_75_out, Input_1);
  not not_76 (not_76_out, Input_2);
  not not_77 (not_77_out, Input_3);
  not not_78 (not_78_out, Input_1);
  not not_79 (not_79_out, Input_3);
  not not_80 (not_80_out, Input_5);
  not not_81 (not_81_out, Input_1);
  not not_82 (not_82_out, Input_3);
  not not_83 (not_83_out, Input_1);
  not not_84 (not_84_out, Input_4);
  not not_85 (not_85_out, Input_5);
  not not_86 (not_86_out, Input_2);
  not not_87 (not_87_out, Input_4);
  not not_88 (not_88_out, Input_2);
  not not_89 (not_89_out, Input_6);
  not not_90 (not_90_out, Input_3);
  not not_91 (not_91_out, Input_4);
  not not_92 (not_92_out, Input_6);
  not not_93 (not_93_out, Input_1);
  not not_94 (not_94_out, Input_2);
  not not_95 (not_95_out, Input_3);
  not not_96 (not_96_out, Input_4);
  not not_97 (not_97_out, Input_6);
  not not_98 (not_98_out, Input_2);
  not not_99 (not_99_out, Input_3);
  not not_100 (not_100_out, Input_4);
  not not_101 (not_101_out, Input_2);
  not not_102 (not_102_out, Input_3);
  not not_103 (not_103_out, Input_6);
  not not_104 (not_104_out, Input_1);
  not not_105 (not_105_out, Input_2);
  not not_106 (not_106_out, Input_5);
  not not_107 (not_107_out, Input_1);
  not not_108 (not_108_out, Input_2);
  not not_109 (not_109_out, Input_5);
  not not_110 (not_110_out, Input_1);
  not not_111 (not_111_out, Input_5);
  not not_112 (not_112_out, Input_2);
  not not_113 (not_113_out, Input_5);
  not not_114 (not_114_out, Input_1);
  not not_115 (not_115_out, Input_1);
  not not_116 (not_116_out, Input_4);
  not not_117 (not_117_out, Input_5);
  not not_118 (not_118_out, Input_1);
  not not_119 (not_119_out, Input_3);
  not not_120 (not_120_out, Input_6);
  not not_121 (not_121_out, Input_2);
  not not_122 (not_122_out, Input_3);
  not not_123 (not_123_out, Input_4);
  not not_124 (not_124_out, Input_2);
  not not_125 (not_125_out, Input_3);
  not not_126 (not_126_out, Input_6);
  not not_127 (not_127_out, Input_3);
  not not_128 (not_128_out, Input_4);
  not not_129 (not_129_out, Input_1);
  not not_130 (not_130_out, Input_3);
  not not_131 (not_131_out, Input_4);
  not not_132 (not_132_out, Input_6);
  not not_133 (not_133_out, Input_1);
  not not_134 (not_134_out, Input_4);
  not not_135 (not_135_out, Input_5);
  not not_136 (not_136_out, Input_6);
  not not_137 (not_137_out, Input_1);
  not not_138 (not_138_out, Input_3);
  not not_139 (not_139_out, Input_6);
  not not_140 (not_140_out, Input_1);
  not not_141 (not_141_out, Input_2);
  not not_142 (not_142_out, Input_1);
  not not_143 (not_143_out, Input_2);
  not not_144 (not_144_out, Input_2);
  not not_145 (not_145_out, Input_1);
  not not_146 (not_146_out, Input_3);
  not not_147 (not_147_out, Input_1);
  not not_148 (not_148_out, Input_4);
  not not_149 (not_149_out, Input_5);
  not not_150 (not_150_out, Input_1);
  not not_151 (not_151_out, Input_6);
  not not_152 (not_152_out, Input_3);
  not not_153 (not_153_out, Input_5);
  not not_154 (not_154_out, Input_6);
  not not_155 (not_155_out, Input_1);
  not not_156 (not_156_out, Input_2);
  not not_157 (not_157_out, Input_3);
  not not_158 (not_158_out, Input_4);
  not not_159 (not_159_out, Input_5);
  not not_160 (not_160_out, Input_1);
  not not_161 (not_161_out, Input_2);
  not not_162 (not_162_out, Input_5);
  not not_163 (not_163_out, Input_6);
  not not_164 (not_164_out, Input_1);
  not not_165 (not_165_out, Input_5);
  not not_166 (not_166_out, Input_1);
  not not_167 (not_167_out, Input_2);
  not not_168 (not_168_out, Input_1);
  not not_169 (not_169_out, Input_3);
  not not_170 (not_170_out, Input_4);
  not not_171 (not_171_out, Input_1);
  not not_172 (not_172_out, Input_3);
  not not_173 (not_173_out, Input_1);
  not not_174 (not_174_out, Input_4);
  not not_175 (not_175_out, Input_1);
  not not_176 (not_176_out, Input_6);
  not not_177 (not_177_out, Input_3);
  not not_178 (not_178_out, Input_5);
  not not_179 (not_179_out, Input_2);
  not not_180 (not_180_out, Input_4);
  not not_181 (not_181_out, Input_2);
  not not_182 (not_182_out, Input_6);
  not not_183 (not_183_out, Input_2);
  not not_184 (not_184_out, Input_3);
  not not_185 (not_185_out, Input_4);
  not not_186 (not_186_out, Input_1);
  not not_187 (not_187_out, Input_2);
  not not_188 (not_188_out, Input_6);
  not not_189 (not_189_out, Input_2);
  not not_190 (not_190_out, Input_5);
  not not_191 (not_191_out, Input_6);
  not not_192 (not_192_out, Input_1);
  not not_193 (not_193_out, Input_3);
  not not_194 (not_194_out, Input_5);
  not not_195 (not_195_out, Input_1);
  not not_196 (not_196_out, Input_4);
  not not_197 (not_197_out, Input_5);
  not not_198 (not_198_out, Input_1);
  not not_199 (not_199_out, Input_4);
  not not_200 (not_200_out, Input_1);
  not not_201 (not_201_out, Input_6);
  not not_202 (not_202_out, Input_1);
  not not_203 (not_203_out, Input_2);
  not not_204 (not_204_out, Input_1);
  not not_205 (not_205_out, Input_4);
  not not_206 (not_206_out, Input_6);
  not not_207 (not_207_out, Input_1);
  not not_208 (not_208_out, Input_5);
  not not_209 (not_209_out, Input_2);
  not not_210 (not_210_out, Input_4);
  not not_211 (not_211_out, Input_2);
  not not_212 (not_212_out, Input_3);
  not not_213 (not_213_out, Input_3);
  not not_214 (not_214_out, Input_6);
  not not_215 (not_215_out, Input_2);
  not not_216 (not_216_out, Input_3);
  not not_217 (not_217_out, Input_5);
  not not_218 (not_218_out, Input_2);
  not not_219 (not_219_out, Input_4);
  not not_220 (not_220_out, Input_5);
  not not_221 (not_221_out, Input_3);
  and and_1 (and_1_out, not_1_out, not_2_out, not_3_out, not_4_out, not_5_out);
  and and_2 (and_2_out, not_6_out, not_7_out, not_8_out, Input_5);
  and and_3 (and_3_out, not_9_out, not_10_out, Input_4, Input_6);
  and and_4 (and_4_out, not_11_out, Input_4, not_12_out, Input_6);
  and and_5 (and_5_out, not_13_out, not_14_out, Input_3, Input_6);
  and and_6 (and_6_out, not_15_out, Input_3, not_16_out, Input_6);
  and and_7 (and_7_out, not_17_out, Input_2, not_18_out, not_19_out, not_20_out);
  and and_8 (and_8_out, Input_2, not_21_out, not_22_out, not_23_out, not_24_out);
  and and_9 (and_9_out, not_25_out, Input_2, Input_3, not_26_out, Input_5);
  and and_10 (and_10_out, Input_1, not_27_out, not_28_out, Input_5, not_29_out);
  and and_11 (and_11_out, not_30_out, not_31_out, not_32_out);
  and and_12 (and_12_out, not_33_out, not_34_out, not_35_out, Input_6);
  and and_13 (and_13_out, not_36_out, not_37_out, not_38_out, Input_6);
  and and_14 (and_14_out, not_39_out, not_40_out, not_41_out, Input_5, not_42_out);
  and and_15 (and_15_out, not_43_out, not_44_out, Input_4, not_45_out, not_46_out);
  and and_16 (and_16_out, not_47_out, not_48_out, Input_4, Input_5, not_49_out);
  and and_17 (and_17_out, not_50_out, not_51_out, Input_4, Input_5, Input_6);
  and and_18 (and_18_out, not_52_out, Input_2, Input_3, not_53_out, Input_5);
  and and_19 (and_19_out, Input_1, not_54_out, not_55_out, not_56_out, Input_6);
  and and_20 (and_20_out, Input_1, not_57_out, Input_3, not_58_out, not_59_out);
  and and_21 (and_21_out, Input_1, not_60_out, Input_3, Input_4, Input_5, Input_6);
  and and_22 (and_22_out, not_61_out, not_62_out, not_63_out, not_64_out);
  and and_23 (and_23_out, not_65_out, not_66_out, not_67_out, not_68_out);
  and and_24 (and_24_out, not_69_out, not_70_out, not_71_out, Input_6);
  and and_25 (and_25_out, not_72_out, not_73_out, not_74_out, Input_6);
  and and_26 (and_26_out, not_75_out, not_76_out, not_77_out, Input_4);
  and and_27 (and_27_out, not_78_out, not_79_out, Input_4, not_80_out);
  and and_28 (and_28_out, not_81_out, not_82_out, Input_4, Input_6);
  and and_29 (and_29_out, not_83_out, Input_3, not_84_out, not_85_out);
  and and_30 (and_30_out, not_86_out, Input_3, not_87_out, Input_6);
  and and_31 (and_31_out, not_88_out, Input_3, Input_4, Input_5, not_89_out);
  and and_32 (and_32_out, Input_2, not_90_out, not_91_out, Input_5, not_92_out);
  and and_33 (and_33_out, not_93_out, Input_2, Input_3, Input_6);
  and and_34 (and_34_out, not_94_out, not_95_out, not_96_out, not_97_out);
  and and_35 (and_35_out, not_98_out, not_99_out, not_100_out, Input_5);
  and and_36 (and_36_out, not_101_out, not_102_out, Input_5, not_103_out);
  and and_37 (and_37_out, not_104_out, not_105_out, Input_4, not_106_out, Input_6);
  and and_38 (and_38_out, not_107_out, not_108_out, Input_3, not_109_out);
  and and_39 (and_39_out, not_110_out, Input_3, not_111_out, Input_6);
  and and_40 (and_40_out, not_112_out, Input_3, Input_4, not_113_out, Input_6);
  and and_41 (and_41_out, not_114_out, Input_3, Input_4, Input_5);
  and and_42 (and_42_out, not_115_out, Input_2, not_116_out, not_117_out, Input_6);
  and and_43 (and_43_out, not_118_out, Input_2, not_119_out, Input_4, not_120_out);
  and and_44 (and_44_out, Input_1, not_121_out, not_122_out, not_123_out);
  and and_45 (and_45_out, Input_1, not_124_out, not_125_out, not_126_out);
  and and_46 (and_46_out, Input_1, not_127_out, not_128_out, Input_5, Input_6);
  and and_47 (and_47_out, not_129_out, not_130_out, not_131_out, not_132_out);
  and and_48 (and_48_out, not_133_out, not_134_out, not_135_out, not_136_out);
  and and_49 (and_49_out, not_137_out, not_138_out, Input_5, not_139_out);
  and and_50 (and_50_out, not_140_out, not_141_out, Input_3, Input_5, Input_6);
  and and_51 (and_51_out, not_142_out, not_143_out, Input_3, Input_4);
  and and_52 (and_52_out, not_144_out, Input_3, Input_4, Input_5, Input_6);
  and and_53 (and_53_out, not_145_out, Input_2, not_146_out);
  and and_54 (and_54_out, not_147_out, Input_2, not_148_out, not_149_out);
  and and_55 (and_55_out, not_150_out, Input_2, not_151_out);
  and and_56 (and_56_out, Input_2, not_152_out, Input_4, not_153_out, not_154_out);
  and and_57 (and_57_out, not_155_out, Input_2, Input_4, Input_5);
  and and_58 (and_58_out, Input_1, not_156_out, not_157_out, not_158_out, not_159_out);
  and and_59 (and_59_out, not_160_out, not_161_out, not_162_out, not_163_out);
  and and_60 (and_60_out, not_164_out, Input_4, not_165_out, Input_6);
  and and_61 (and_61_out, not_166_out, not_167_out, Input_3, Input_6);
  and and_62 (and_62_out, not_168_out, Input_2, not_169_out, not_170_out);
  and and_63 (and_63_out, not_171_out, Input_2, not_172_out, Input_5);
  and and_64 (and_64_out, not_173_out, Input_2, not_174_out, Input_5);
  and and_65 (and_65_out, not_175_out, Input_2, Input_5, not_176_out);
  and and_66 (and_66_out, Input_2, not_177_out, Input_4, not_178_out, Input_6);
  and and_67 (and_67_out, Input_1, not_179_out, not_180_out, Input_6);
  and and_68 (and_68_out, Input_1, not_181_out, Input_3, Input_5, not_182_out);
  and and_69 (and_69_out, not_183_out, not_184_out, not_185_out, Input_5);
  and and_70 (and_70_out, not_186_out, not_187_out, Input_4, not_188_out);
  and and_71 (and_71_out, not_189_out, Input_4, not_190_out, not_191_out);
  and and_72 (and_72_out, not_192_out, not_193_out, Input_4, not_194_out, Input_6);
  and and_73 (and_73_out, not_195_out, Input_3, not_196_out, not_197_out);
  and and_74 (and_74_out, not_198_out, Input_3, not_199_out, Input_6);
  and and_75 (and_75_out, not_200_out, Input_3, Input_4, not_201_out);
  and and_76 (and_76_out, not_202_out, not_203_out, Input_3, Input_4, Input_5);
  and and_77 (and_77_out, not_204_out, Input_2, not_205_out, not_206_out);
  and and_78 (and_78_out, not_207_out, Input_2, Input_3, not_208_out);
  and and_79 (and_79_out, Input_1, not_209_out, not_210_out, Input_5);
  and and_80 (and_80_out, Input_1, not_211_out, not_212_out, Input_5, Input_6);
  and and_81 (and_81_out, Input_1, Input_2, not_213_out, Input_4, Input_5, not_214_out);
  and and_82 (and_82_out, Input_1, not_215_out, not_216_out, Input_4, not_217_out, Input_6);
  and and_83 (and_83_out, Input_1, not_218_out, Input_3, not_219_out, not_220_out);
  and and_84 (and_84_out, Input_1, Input_2, not_221_out, Input_4, Input_5, Input_6);
  or or_1 (Output_1, and_1_out, and_2_out, and_3_out, and_4_out, and_5_out, and_6_out, and_7_out, and_8_out, and_9_out, and_10_out);
  or or_2 (Output_2, and_11_out, and_12_out, and_13_out, and_14_out, and_15_out, and_16_out, and_17_out, and_18_out, and_19_out, and_20_out, and_21_out);
  or or_3 (Output_3, and_22_out, and_23_out, and_24_out, and_25_out, and_26_out, and_27_out, and_28_out, and_29_out, and_30_out, and_31_out, and_32_out, and_33_out);
  or or_4 (Output_4, and_34_out, and_35_out, and_36_out, and_37_out, and_38_out, and_39_out, and_40_out, and_41_out, and_42_out, and_43_out, and_44_out, and_45_out, and_46_out);
  or or_5 (Output_5, and_47_out, and_48_out, and_49_out, and_50_out, and_51_out, and_52_out, and_53_out, and_54_out, and_55_out, and_56_out, and_57_out, and_58_out);
  or or_6 (Output_6, and_59_out, and_60_out, and_61_out, and_62_out, and_63_out, and_64_out, and_65_out, and_66_out, and_67_out, and_68_out);
  or or_7 (Output_7, and_69_out, and_70_out, and_71_out, and_72_out, and_73_out, and_74_out, and_75_out, and_76_out, and_77_out, and_78_out, and_79_out, and_80_out, and_81_out);
  or or_8 (Output_8, and_82_out, and_83_out, and_84_out);
endmodule
module rectifieurhorraire (
  input  bh0,
  input  bh1,
  input  bh2,
  input  bh3,
  input  bh4,
  input  sh0,
  input  sh1,
  input  sh2,
  input  sh3,
  input  sh4,
  output h0,
  output h1,
  output h2,
  output h3,
  output h4
);

  wire and_1_out, and_2_out, and_3_out, and_4_out, and_5_out, and_6_out, and_7_out, and_8_out, and_9_out,
       and_10_out, and_11_out, and_12_out, and_13_out, and_14_out, and_15_out, and_16_out, and_17_out,
       and_18_out, and_19_out, and_20_out, and_21_out, and_22_out, and_23_out, and_24_out, and_25_out,
       and_26_out, and_27_out, and_28_out, and_29_out, and_30_out, and_31_out, and_32_out, and_33_out,
       and_34_out, and_35_out, and_36_out, and_37_out, and_38_out, and_39_out, and_40_out, and_41_out,
       and_42_out, and_43_out, and_44_out, and_45_out, and_46_out, and_47_out, and_48_out, and_49_out,
       and_50_out, and_51_out, and_52_out, and_53_out, and_54_out, and_55_out, and_56_out, and_57_out,
       and_58_out, and_59_out, and_60_out, and_61_out, and_62_out, and_63_out, and_64_out, and_65_out,
       and_66_out, and_67_out, and_68_out, and_69_out, and_70_out, and_71_out, and_72_out, and_73_out,
       and_74_out, and_75_out, and_76_out, and_77_out, and_78_out, and_79_out, and_80_out, and_81_out,
       and_82_out, and_83_out, and_84_out, and_85_out, and_86_out, and_87_out, and_88_out, and_89_out,
       and_90_out, and_91_out, and_92_out, and_93_out, and_94_out, and_95_out, and_96_out, and_97_out,
       and_98_out, and_99_out, and_100_out, and_101_out, and_102_out, and_103_out, and_104_out, and_105_out,
       and_106_out, and_107_out, and_108_out, and_109_out, and_110_out, and_111_out, and_112_out,
       and_113_out, and_114_out, and_115_out, and_116_out, and_117_out, and_118_out, and_119_out,
       and_120_out, and_121_out, and_122_out, and_123_out, and_124_out, and_125_out, and_126_out,
       and_127_out, and_128_out, and_129_out, and_130_out, and_131_out, and_132_out, and_133_out,
       and_134_out, and_135_out, and_136_out, and_137_out, and_138_out, and_139_out, and_140_out,
       and_141_out, and_142_out, and_143_out, and_144_out, and_145_out, and_146_out, and_147_out,
       and_148_out, and_149_out, and_150_out, and_151_out, and_152_out, and_153_out, and_154_out,
       and_155_out, and_156_out, and_157_out, and_158_out, and_159_out, and_160_out, and_161_out,
       and_162_out, and_163_out, and_164_out, and_165_out, and_166_out, and_167_out, and_168_out,
       and_169_out, and_170_out, and_171_out, and_172_out, and_173_out, and_174_out, and_175_out,
       and_176_out, and_177_out, and_178_out, and_179_out, and_180_out, and_181_out, and_182_out,
       and_183_out, and_184_out, and_185_out, and_186_out, and_187_out, and_188_out, and_189_out,
       and_190_out, and_191_out, and_192_out, and_193_out, and_194_out, and_195_out, and_196_out,
       and_197_out, and_198_out, and_199_out, and_200_out, and_201_out, and_202_out, and_203_out,
       and_204_out, and_205_out, and_206_out, and_207_out, and_208_out, and_209_out, and_210_out,
       and_211_out, not_1_out, not_2_out, not_3_out, not_4_out, not_5_out, not_6_out, not_7_out, not_8_out,
       not_9_out, not_10_out, not_11_out, not_12_out, not_13_out, not_14_out, not_15_out, not_16_out,
       not_17_out, not_18_out, not_19_out, not_20_out, not_21_out, not_22_out, not_23_out, not_24_out,
       not_25_out, not_26_out, not_27_out, not_28_out, not_29_out, not_30_out, not_31_out, not_32_out,
       not_33_out, not_34_out, not_35_out, not_36_out, not_37_out, not_38_out, not_39_out, not_40_out,
       not_41_out, not_42_out, not_43_out, not_44_out, not_45_out, not_46_out, not_47_out, not_48_out,
       not_49_out, not_50_out, not_51_out, not_52_out, not_53_out, not_54_out, not_55_out, not_56_out,
       not_57_out, not_58_out, not_59_out, not_60_out, not_61_out, not_62_out, not_63_out, not_64_out,
       not_65_out, not_66_out, not_67_out, not_68_out, not_69_out, not_70_out, not_71_out, not_72_out,
       not_73_out, not_74_out, not_75_out, not_76_out, not_77_out, not_78_out, not_79_out, not_80_out,
       not_81_out, not_82_out, not_83_out, not_84_out, not_85_out, not_86_out, not_87_out, not_88_out,
       not_89_out, not_90_out, not_91_out, not_92_out, not_93_out, not_94_out, not_95_out, not_96_out,
       not_97_out, not_98_out, not_99_out, not_100_out, not_101_out, not_102_out, not_103_out, not_104_out,
       not_105_out, not_106_out, not_107_out, not_108_out, not_109_out, not_110_out, not_111_out,
       not_112_out, not_113_out, not_114_out, not_115_out, not_116_out, not_117_out, not_118_out,
       not_119_out, not_120_out, not_121_out, not_122_out, not_123_out, not_124_out, not_125_out,
       not_126_out, not_127_out, not_128_out, not_129_out, not_130_out, not_131_out, not_132_out,
       not_133_out, not_134_out, not_135_out, not_136_out, not_137_out, not_138_out, not_139_out,
       not_140_out, not_141_out, not_142_out, not_143_out, not_144_out, not_145_out, not_146_out,
       not_147_out, not_148_out, not_149_out, not_150_out, not_151_out, not_152_out, not_153_out,
       not_154_out, not_155_out, not_156_out, not_157_out, not_158_out, not_159_out, not_160_out,
       not_161_out, not_162_out, not_163_out, not_164_out, not_165_out, not_166_out, not_167_out,
       not_168_out, not_169_out, not_170_out, not_171_out, not_172_out, not_173_out, not_174_out,
       not_175_out, not_176_out, not_177_out, not_178_out, not_179_out, not_180_out, not_181_out,
       not_182_out, not_183_out, not_184_out, not_185_out, not_186_out, not_187_out, not_188_out,
       not_189_out, not_190_out, not_191_out, not_192_out, not_193_out, not_194_out, not_195_out,
       not_196_out, not_197_out, not_198_out, not_199_out, not_200_out, not_201_out, not_202_out,
       not_203_out, not_204_out, not_205_out, not_206_out, not_207_out, not_208_out, not_209_out,
       not_210_out, not_211_out, not_212_out, not_213_out, not_214_out, not_215_out, not_216_out,
       not_217_out, not_218_out, not_219_out, not_220_out, not_221_out, not_222_out, not_223_out,
       not_224_out, not_225_out, not_226_out, not_227_out, not_228_out, not_229_out, not_230_out,
       not_231_out, not_232_out, not_233_out, not_234_out, not_235_out, not_236_out, not_237_out,
       not_238_out, not_239_out, not_240_out, not_241_out, not_242_out, not_243_out, not_244_out,
       not_245_out, not_246_out, not_247_out, not_248_out, not_249_out, not_250_out, not_251_out,
       not_252_out, not_253_out, not_254_out, not_255_out, not_256_out, not_257_out, not_258_out,
       not_259_out, not_260_out, not_261_out, not_262_out, not_263_out, not_264_out, not_265_out,
       not_266_out, not_267_out, not_268_out, not_269_out, not_270_out, not_271_out, not_272_out,
       not_273_out, not_274_out, not_275_out, not_276_out, not_277_out, not_278_out, not_279_out,
       not_280_out, not_281_out, not_282_out, not_283_out, not_284_out, not_285_out, not_286_out,
       not_287_out, not_288_out, not_289_out, not_290_out, not_291_out, not_292_out, not_293_out,
       not_294_out, not_295_out, not_296_out, not_297_out, not_298_out, not_299_out, not_300_out,
       not_301_out, not_302_out, not_303_out, not_304_out, not_305_out, not_306_out, not_307_out,
       not_308_out, not_309_out, not_310_out, not_311_out, not_312_out, not_313_out, not_314_out,
       not_315_out, not_316_out, not_317_out, not_318_out, not_319_out, not_320_out, not_321_out,
       not_322_out, not_323_out, not_324_out, not_325_out, not_326_out, not_327_out, not_328_out,
       not_329_out, not_330_out, not_331_out, not_332_out, not_333_out, not_334_out, not_335_out,
       not_336_out, not_337_out, not_338_out, not_339_out, not_340_out, not_341_out, not_342_out,
       not_343_out, not_344_out, not_345_out, not_346_out, not_347_out, not_348_out, not_349_out,
       not_350_out, not_351_out, not_352_out, not_353_out, not_354_out, not_355_out, not_356_out,
       not_357_out, not_358_out, not_359_out, not_360_out, not_361_out, not_362_out, not_363_out,
       not_364_out, not_365_out, not_366_out, not_367_out, not_368_out, not_369_out, not_370_out,
       not_371_out, not_372_out, not_373_out, not_374_out, not_375_out, not_376_out, not_377_out,
       not_378_out, not_379_out, not_380_out, not_381_out, not_382_out, not_383_out, not_384_out,
       not_385_out, not_386_out, not_387_out, not_388_out, not_389_out, not_390_out, not_391_out,
       not_392_out, not_393_out, not_394_out, not_395_out, not_396_out, not_397_out, not_398_out,
       not_399_out, not_400_out, not_401_out, not_402_out, not_403_out, not_404_out, not_405_out,
       not_406_out, not_407_out, not_408_out, not_409_out, not_410_out, not_411_out, not_412_out,
       not_413_out, not_414_out, not_415_out, not_416_out, not_417_out, not_418_out, not_419_out,
       not_420_out, not_421_out, not_422_out, not_423_out, not_424_out, not_425_out, not_426_out,
       not_427_out, not_428_out, not_429_out, not_430_out, not_431_out, not_432_out, not_433_out,
       not_434_out, not_435_out, not_436_out, not_437_out, not_438_out, not_439_out, not_440_out,
       not_441_out, not_442_out, not_443_out, not_444_out, not_445_out, not_446_out, not_447_out,
       not_448_out, not_449_out, not_450_out, not_451_out, not_452_out, not_453_out, not_454_out,
       not_455_out, not_456_out, not_457_out, not_458_out, not_459_out, not_460_out, not_461_out,
       not_462_out, not_463_out, not_464_out, not_465_out, not_466_out, not_467_out, not_468_out,
       not_469_out, not_470_out, not_471_out, not_472_out, not_473_out, not_474_out, not_475_out,
       not_476_out, not_477_out, not_478_out, not_479_out, not_480_out, not_481_out, not_482_out,
       not_483_out, not_484_out, not_485_out, not_486_out, not_487_out, not_488_out, not_489_out,
       not_490_out, not_491_out, not_492_out, not_493_out, not_494_out, not_495_out, not_496_out,
       not_497_out, not_498_out, not_499_out, not_500_out, not_501_out, not_502_out, not_503_out,
       not_504_out, not_505_out, not_506_out, not_507_out, not_508_out, not_509_out, not_510_out,
       not_511_out, not_512_out, not_513_out, not_514_out, not_515_out, not_516_out, not_517_out,
       not_518_out, not_519_out, not_520_out, not_521_out, not_522_out, not_523_out, not_524_out,
       not_525_out, not_526_out, not_527_out, not_528_out, not_529_out, not_530_out, not_531_out,
       not_532_out, not_533_out, not_534_out, not_535_out, not_536_out, not_537_out, not_538_out,
       not_539_out, not_540_out, not_541_out, not_542_out, not_543_out, not_544_out, not_545_out,
       not_546_out, not_547_out, not_548_out, not_549_out, not_550_out, not_551_out, not_552_out,
       not_553_out, not_554_out, not_555_out, not_556_out, not_557_out, not_558_out, not_559_out,
       not_560_out, not_561_out, not_562_out, not_563_out, not_564_out, not_565_out, not_566_out,
       not_567_out, not_568_out, not_569_out, not_570_out, not_571_out, not_572_out, not_573_out,
       not_574_out, not_575_out, not_576_out, not_577_out, not_578_out, not_579_out, not_580_out,
       not_581_out, not_582_out, not_583_out, not_584_out, not_585_out, not_586_out, not_587_out,
       not_588_out, not_589_out, not_590_out, not_591_out, not_592_out, not_593_out, not_594_out,
       not_595_out, not_596_out, not_597_out, not_598_out, not_599_out, not_600_out, not_601_out,
       not_602_out, not_603_out, not_604_out, not_605_out, not_606_out, not_607_out, not_608_out,
       not_609_out, not_610_out, not_611_out, not_612_out, not_613_out, not_614_out, not_615_out,
       not_616_out, not_617_out, not_618_out, not_619_out, not_620_out, not_621_out, not_622_out,
       not_623_out, not_624_out, not_625_out, not_626_out, not_627_out, not_628_out, not_629_out,
       not_630_out, not_631_out, not_632_out, not_633_out, not_634_out, not_635_out, not_636_out,
       not_637_out, not_638_out, not_639_out, not_640_out, not_641_out, not_642_out, not_643_out,
       not_644_out, not_645_out, not_646_out, not_647_out, not_648_out, not_649_out, not_650_out,
       not_651_out, not_652_out, not_653_out, not_654_out, not_655_out, not_656_out, not_657_out,
       not_658_out, not_659_out, not_660_out, not_661_out, not_662_out, not_663_out, not_664_out,
       not_665_out, not_666_out, not_667_out, not_668_out, not_669_out, not_670_out, not_671_out,
       not_672_out, not_673_out, not_674_out, not_675_out, not_676_out, not_677_out, not_678_out,
       not_679_out, not_680_out, not_681_out, not_682_out, not_683_out, not_684_out, not_685_out,
       not_686_out, not_687_out, not_688_out, not_689_out, not_690_out, not_691_out, not_692_out,
       not_693_out, not_694_out, not_695_out, not_696_out, not_697_out, not_698_out, not_699_out,
       not_700_out, not_701_out, not_702_out, not_703_out, not_704_out, not_705_out, not_706_out,
       not_707_out, not_708_out, not_709_out, not_710_out, not_711_out, not_712_out, not_713_out,
       not_714_out, not_715_out, not_716_out, not_717_out, not_718_out, not_719_out, not_720_out,
       not_721_out, not_722_out, not_723_out, not_724_out, not_725_out, not_726_out, not_727_out,
       not_728_out, not_729_out, not_730_out, not_731_out, not_732_out, not_733_out, not_734_out,
       not_735_out, not_736_out, not_737_out, not_738_out, not_739_out, not_740_out, not_741_out,
       not_742_out, or_4_out, or_5_out, or_6_out, or_7_out, or_8_out, or_10_out, or_11_out;

  not not_1 (not_1_out, bh0);
  not not_2 (not_2_out, bh1);
  not not_3 (not_3_out, bh2);
  not not_4 (not_4_out, bh3);
  not not_5 (not_5_out, bh4);
  not not_6 (not_6_out, sh1);
  not not_7 (not_7_out, bh0);
  not not_8 (not_8_out, bh1);
  not not_9 (not_9_out, bh2);
  not not_10 (not_10_out, bh3);
  not not_11 (not_11_out, sh1);
  not not_12 (not_12_out, sh3);
  not not_13 (not_13_out, bh0);
  not not_14 (not_14_out, bh1);
  not not_15 (not_15_out, bh2);
  not not_16 (not_16_out, bh3);
  not not_17 (not_17_out, sh1);
  not not_18 (not_18_out, sh4);
  not not_19 (not_19_out, bh0);
  not not_20 (not_20_out, bh1);
  not not_21 (not_21_out, bh2);
  not not_22 (not_22_out, bh4);
  not not_23 (not_23_out, sh1);
  not not_24 (not_24_out, sh3);
  not not_25 (not_25_out, bh0);
  not not_26 (not_26_out, bh1);
  not not_27 (not_27_out, bh2);
  not not_28 (not_28_out, sh1);
  not not_29 (not_29_out, sh2);
  not not_30 (not_30_out, bh0);
  not not_31 (not_31_out, bh1);
  not not_32 (not_32_out, bh2);
  not not_33 (not_33_out, sh1);
  not not_34 (not_34_out, sh3);
  not not_35 (not_35_out, sh4);
  not not_36 (not_36_out, bh0);
  not not_37 (not_37_out, bh1);
  not not_38 (not_38_out, bh3);
  not not_39 (not_39_out, bh4);
  not not_40 (not_40_out, sh1);
  not not_41 (not_41_out, sh2);
  not not_42 (not_42_out, bh0);
  not not_43 (not_43_out, bh1);
  not not_44 (not_44_out, bh3);
  not not_45 (not_45_out, sh1);
  not not_46 (not_46_out, sh2);
  not not_47 (not_47_out, sh3);
  not not_48 (not_48_out, bh0);
  not not_49 (not_49_out, bh1);
  not not_50 (not_50_out, bh3);
  not not_51 (not_51_out, sh1);
  not not_52 (not_52_out, sh2);
  not not_53 (not_53_out, sh4);
  not not_54 (not_54_out, bh0);
  not not_55 (not_55_out, bh1);
  not not_56 (not_56_out, bh4);
  not not_57 (not_57_out, sh1);
  not not_58 (not_58_out, sh2);
  not not_59 (not_59_out, sh3);
  not not_60 (not_60_out, bh0);
  not not_61 (not_61_out, bh1);
  not not_62 (not_62_out, sh1);
  not not_63 (not_63_out, sh2);
  not not_64 (not_64_out, sh3);
  not not_65 (not_65_out, sh4);
  not not_66 (not_66_out, bh0);
  not not_67 (not_67_out, bh1);
  not not_68 (not_68_out, sh0);
  not not_69 (not_69_out, bh0);
  not not_70 (not_70_out, bh1);
  not not_71 (not_71_out, sh0);
  not not_72 (not_72_out, bh0);
  not not_73 (not_73_out, bh1);
  not not_74 (not_74_out, sh0);
  not not_75 (not_75_out, bh0);
  not not_76 (not_76_out, bh1);
  not not_77 (not_77_out, sh0);
  not not_78 (not_78_out, bh0);
  not not_79 (not_79_out, bh1);
  not not_80 (not_80_out, sh0);
  not not_81 (not_81_out, bh0);
  not not_82 (not_82_out, bh1);
  not not_83 (not_83_out, sh0);
  not not_84 (not_84_out, bh0);
  not not_85 (not_85_out, bh1);
  not not_86 (not_86_out, sh0);
  not not_87 (not_87_out, bh0);
  not not_88 (not_88_out, bh2);
  not not_89 (not_89_out, bh3);
  not not_90 (not_90_out, bh4);
  not not_91 (not_91_out, sh0);
  not not_92 (not_92_out, bh0);
  not not_93 (not_93_out, bh2);
  not not_94 (not_94_out, bh3);
  not not_95 (not_95_out, sh0);
  not not_96 (not_96_out, sh3);
  not not_97 (not_97_out, bh0);
  not not_98 (not_98_out, bh2);
  not not_99 (not_99_out, bh3);
  not not_100 (not_100_out, sh0);
  not not_101 (not_101_out, sh4);
  not not_102 (not_102_out, bh0);
  not not_103 (not_103_out, bh2);
  not not_104 (not_104_out, bh4);
  not not_105 (not_105_out, sh0);
  not not_106 (not_106_out, sh3);
  not not_107 (not_107_out, bh0);
  not not_108 (not_108_out, bh2);
  not not_109 (not_109_out, sh0);
  not not_110 (not_110_out, sh2);
  not not_111 (not_111_out, bh0);
  not not_112 (not_112_out, bh2);
  not not_113 (not_113_out, sh0);
  not not_114 (not_114_out, sh3);
  not not_115 (not_115_out, sh4);
  not not_116 (not_116_out, bh0);
  not not_117 (not_117_out, bh3);
  not not_118 (not_118_out, bh4);
  not not_119 (not_119_out, sh0);
  not not_120 (not_120_out, sh2);
  not not_121 (not_121_out, bh0);
  not not_122 (not_122_out, bh3);
  not not_123 (not_123_out, sh0);
  not not_124 (not_124_out, sh2);
  not not_125 (not_125_out, sh3);
  not not_126 (not_126_out, bh0);
  not not_127 (not_127_out, bh3);
  not not_128 (not_128_out, sh0);
  not not_129 (not_129_out, sh2);
  not not_130 (not_130_out, sh4);
  not not_131 (not_131_out, bh0);
  not not_132 (not_132_out, bh4);
  not not_133 (not_133_out, sh0);
  not not_134 (not_134_out, sh2);
  not not_135 (not_135_out, sh3);
  not not_136 (not_136_out, bh0);
  not not_137 (not_137_out, sh0);
  not not_138 (not_138_out, sh2);
  not not_139 (not_139_out, sh3);
  not not_140 (not_140_out, sh4);
  not not_141 (not_141_out, bh0);
  not not_142 (not_142_out, sh0);
  not not_143 (not_143_out, sh1);
  not not_144 (not_144_out, bh0);
  not not_145 (not_145_out, bh0);
  not not_146 (not_146_out, sh0);
  not not_147 (not_147_out, sh1);
  not not_148 (not_148_out, bh0);
  not not_149 (not_149_out, bh0);
  not not_150 (not_150_out, sh0);
  not not_151 (not_151_out, sh1);
  not not_152 (not_152_out, bh0);
  not not_153 (not_153_out, bh0);
  not not_154 (not_154_out, sh0);
  not not_155 (not_155_out, sh1);
  not not_156 (not_156_out, bh0);
  not not_157 (not_157_out, bh0);
  not not_158 (not_158_out, sh0);
  not not_159 (not_159_out, sh1);
  not not_160 (not_160_out, bh0);
  not not_161 (not_161_out, bh0);
  not not_162 (not_162_out, sh0);
  not not_163 (not_163_out, sh1);
  not not_164 (not_164_out, bh0);
  not not_165 (not_165_out, bh0);
  not not_166 (not_166_out, sh0);
  not not_167 (not_167_out, sh1);
  not not_168 (not_168_out, bh0);
  not not_169 (not_169_out, bh1);
  not not_170 (not_170_out, bh2);
  not not_171 (not_171_out, bh3);
  not not_172 (not_172_out, bh4);
  not not_173 (not_173_out, sh0);
  not not_174 (not_174_out, sh1);
  not not_175 (not_175_out, bh1);
  not not_176 (not_176_out, bh2);
  not not_177 (not_177_out, bh3);
  not not_178 (not_178_out, sh0);
  not not_179 (not_179_out, sh1);
  not not_180 (not_180_out, sh3);
  not not_181 (not_181_out, bh1);
  not not_182 (not_182_out, bh2);
  not not_183 (not_183_out, bh3);
  not not_184 (not_184_out, sh0);
  not not_185 (not_185_out, sh1);
  not not_186 (not_186_out, sh4);
  not not_187 (not_187_out, bh1);
  not not_188 (not_188_out, bh2);
  not not_189 (not_189_out, bh4);
  not not_190 (not_190_out, sh0);
  not not_191 (not_191_out, sh1);
  not not_192 (not_192_out, sh3);
  not not_193 (not_193_out, bh1);
  not not_194 (not_194_out, bh2);
  not not_195 (not_195_out, sh0);
  not not_196 (not_196_out, sh1);
  not not_197 (not_197_out, sh2);
  not not_198 (not_198_out, bh1);
  not not_199 (not_199_out, bh2);
  not not_200 (not_200_out, sh0);
  not not_201 (not_201_out, sh1);
  not not_202 (not_202_out, sh3);
  not not_203 (not_203_out, sh4);
  not not_204 (not_204_out, bh1);
  not not_205 (not_205_out, bh3);
  not not_206 (not_206_out, bh4);
  not not_207 (not_207_out, sh0);
  not not_208 (not_208_out, sh1);
  not not_209 (not_209_out, sh2);
  not not_210 (not_210_out, bh1);
  not not_211 (not_211_out, bh3);
  not not_212 (not_212_out, sh0);
  not not_213 (not_213_out, sh1);
  not not_214 (not_214_out, sh2);
  not not_215 (not_215_out, sh3);
  not not_216 (not_216_out, bh1);
  not not_217 (not_217_out, bh3);
  not not_218 (not_218_out, sh0);
  not not_219 (not_219_out, sh1);
  not not_220 (not_220_out, sh2);
  not not_221 (not_221_out, sh4);
  not not_222 (not_222_out, bh1);
  not not_223 (not_223_out, bh4);
  not not_224 (not_224_out, sh0);
  not not_225 (not_225_out, sh1);
  not not_226 (not_226_out, sh2);
  not not_227 (not_227_out, sh3);
  not not_228 (not_228_out, bh1);
  not not_229 (not_229_out, sh0);
  not not_230 (not_230_out, sh1);
  not not_231 (not_231_out, sh2);
  not not_232 (not_232_out, sh3);
  not not_233 (not_233_out, sh4);
  not not_234 (not_234_out, bh1);
  not not_235 (not_235_out, bh2);
  not not_236 (not_236_out, bh3);
  not not_237 (not_237_out, bh4);
  not not_238 (not_238_out, bh1);
  not not_239 (not_239_out, bh2);
  not not_240 (not_240_out, bh3);
  not not_241 (not_241_out, sh3);
  not not_242 (not_242_out, bh1);
  not not_243 (not_243_out, bh2);
  not not_244 (not_244_out, bh3);
  not not_245 (not_245_out, sh4);
  not not_246 (not_246_out, bh1);
  not not_247 (not_247_out, bh2);
  not not_248 (not_248_out, bh4);
  not not_249 (not_249_out, sh3);
  not not_250 (not_250_out, bh1);
  not not_251 (not_251_out, bh2);
  not not_252 (not_252_out, sh2);
  not not_253 (not_253_out, bh1);
  not not_254 (not_254_out, bh2);
  not not_255 (not_255_out, sh3);
  not not_256 (not_256_out, sh4);
  not not_257 (not_257_out, bh1);
  not not_258 (not_258_out, bh3);
  not not_259 (not_259_out, bh4);
  not not_260 (not_260_out, sh2);
  not not_261 (not_261_out, bh1);
  not not_262 (not_262_out, bh3);
  not not_263 (not_263_out, sh2);
  not not_264 (not_264_out, sh3);
  not not_265 (not_265_out, bh1);
  not not_266 (not_266_out, bh3);
  not not_267 (not_267_out, sh2);
  not not_268 (not_268_out, sh4);
  not not_269 (not_269_out, bh1);
  not not_270 (not_270_out, bh4);
  not not_271 (not_271_out, sh2);
  not not_272 (not_272_out, sh3);
  not not_273 (not_273_out, bh1);
  not not_274 (not_274_out, sh2);
  not not_275 (not_275_out, sh3);
  not not_276 (not_276_out, sh4);
  not not_277 (not_277_out, bh1);
  not not_278 (not_278_out, sh1);
  not not_279 (not_279_out, bh1);
  not not_280 (not_280_out, sh1);
  not not_281 (not_281_out, bh1);
  not not_282 (not_282_out, sh1);
  not not_283 (not_283_out, bh1);
  not not_284 (not_284_out, sh1);
  not not_285 (not_285_out, bh1);
  not not_286 (not_286_out, sh1);
  not not_287 (not_287_out, bh1);
  not not_288 (not_288_out, sh1);
  not not_289 (not_289_out, bh1);
  not not_290 (not_290_out, sh1);
  not not_291 (not_291_out, bh2);
  not not_292 (not_292_out, bh3);
  not not_293 (not_293_out, bh4);
  not not_294 (not_294_out, sh1);
  not not_295 (not_295_out, bh2);
  not not_296 (not_296_out, bh3);
  not not_297 (not_297_out, sh1);
  not not_298 (not_298_out, sh3);
  not not_299 (not_299_out, bh2);
  not not_300 (not_300_out, bh3);
  not not_301 (not_301_out, sh1);
  not not_302 (not_302_out, sh4);
  not not_303 (not_303_out, bh2);
  not not_304 (not_304_out, bh4);
  not not_305 (not_305_out, sh1);
  not not_306 (not_306_out, sh3);
  not not_307 (not_307_out, bh2);
  not not_308 (not_308_out, sh1);
  not not_309 (not_309_out, sh2);
  not not_310 (not_310_out, bh2);
  not not_311 (not_311_out, sh1);
  not not_312 (not_312_out, sh3);
  not not_313 (not_313_out, sh4);
  not not_314 (not_314_out, bh3);
  not not_315 (not_315_out, bh4);
  not not_316 (not_316_out, sh1);
  not not_317 (not_317_out, sh2);
  not not_318 (not_318_out, bh3);
  not not_319 (not_319_out, sh1);
  not not_320 (not_320_out, sh2);
  not not_321 (not_321_out, sh3);
  not not_322 (not_322_out, bh3);
  not not_323 (not_323_out, sh1);
  not not_324 (not_324_out, sh2);
  not not_325 (not_325_out, sh4);
  not not_326 (not_326_out, bh4);
  not not_327 (not_327_out, sh1);
  not not_328 (not_328_out, sh2);
  not not_329 (not_329_out, sh3);
  not not_330 (not_330_out, sh1);
  not not_331 (not_331_out, sh2);
  not not_332 (not_332_out, sh3);
  not not_333 (not_333_out, sh4);
  not not_334 (not_334_out, sh0);
  not not_335 (not_335_out, sh0);
  not not_336 (not_336_out, sh0);
  not not_337 (not_337_out, sh0);
  not not_338 (not_338_out, sh0);
  not not_339 (not_339_out, sh0);
  not not_340 (not_340_out, sh0);
  not not_341 (not_341_out, bh0);
  not not_342 (not_342_out, bh1);
  not not_343 (not_343_out, bh2);
  not not_344 (not_344_out, bh3);
  not not_345 (not_345_out, bh4);
  not not_346 (not_346_out, sh0);
  not not_347 (not_347_out, bh0);
  not not_348 (not_348_out, bh1);
  not not_349 (not_349_out, bh2);
  not not_350 (not_350_out, bh3);
  not not_351 (not_351_out, sh0);
  not not_352 (not_352_out, sh3);
  not not_353 (not_353_out, bh0);
  not not_354 (not_354_out, bh1);
  not not_355 (not_355_out, bh2);
  not not_356 (not_356_out, bh3);
  not not_357 (not_357_out, sh0);
  not not_358 (not_358_out, sh4);
  not not_359 (not_359_out, bh0);
  not not_360 (not_360_out, bh1);
  not not_361 (not_361_out, bh2);
  not not_362 (not_362_out, bh4);
  not not_363 (not_363_out, sh0);
  not not_364 (not_364_out, sh3);
  not not_365 (not_365_out, bh0);
  not not_366 (not_366_out, bh1);
  not not_367 (not_367_out, bh2);
  not not_368 (not_368_out, sh0);
  not not_369 (not_369_out, sh2);
  not not_370 (not_370_out, bh0);
  not not_371 (not_371_out, bh1);
  not not_372 (not_372_out, bh2);
  not not_373 (not_373_out, sh0);
  not not_374 (not_374_out, sh3);
  not not_375 (not_375_out, sh4);
  not not_376 (not_376_out, bh0);
  not not_377 (not_377_out, bh1);
  not not_378 (not_378_out, bh3);
  not not_379 (not_379_out, bh4);
  not not_380 (not_380_out, sh0);
  not not_381 (not_381_out, sh2);
  not not_382 (not_382_out, bh0);
  not not_383 (not_383_out, bh1);
  not not_384 (not_384_out, bh3);
  not not_385 (not_385_out, sh0);
  not not_386 (not_386_out, sh2);
  not not_387 (not_387_out, sh3);
  not not_388 (not_388_out, bh0);
  not not_389 (not_389_out, bh1);
  not not_390 (not_390_out, bh3);
  not not_391 (not_391_out, sh0);
  not not_392 (not_392_out, sh2);
  not not_393 (not_393_out, sh4);
  not not_394 (not_394_out, bh0);
  not not_395 (not_395_out, bh1);
  not not_396 (not_396_out, bh4);
  not not_397 (not_397_out, sh0);
  not not_398 (not_398_out, sh2);
  not not_399 (not_399_out, sh3);
  not not_400 (not_400_out, bh0);
  not not_401 (not_401_out, bh1);
  not not_402 (not_402_out, sh0);
  not not_403 (not_403_out, sh2);
  not not_404 (not_404_out, sh3);
  not not_405 (not_405_out, sh4);
  not not_406 (not_406_out, bh0);
  not not_407 (not_407_out, bh1);
  not not_408 (not_408_out, sh0);
  not not_409 (not_409_out, sh1);
  not not_410 (not_410_out, bh0);
  not not_411 (not_411_out, bh1);
  not not_412 (not_412_out, bh0);
  not not_413 (not_413_out, bh1);
  not not_414 (not_414_out, sh0);
  not not_415 (not_415_out, sh1);
  not not_416 (not_416_out, bh0);
  not not_417 (not_417_out, bh1);
  not not_418 (not_418_out, bh0);
  not not_419 (not_419_out, bh1);
  not not_420 (not_420_out, sh0);
  not not_421 (not_421_out, sh1);
  not not_422 (not_422_out, bh0);
  not not_423 (not_423_out, bh1);
  not not_424 (not_424_out, bh0);
  not not_425 (not_425_out, bh1);
  not not_426 (not_426_out, sh0);
  not not_427 (not_427_out, sh1);
  not not_428 (not_428_out, bh0);
  not not_429 (not_429_out, bh1);
  not not_430 (not_430_out, bh0);
  not not_431 (not_431_out, bh1);
  not not_432 (not_432_out, sh0);
  not not_433 (not_433_out, sh1);
  not not_434 (not_434_out, bh0);
  not not_435 (not_435_out, bh1);
  not not_436 (not_436_out, bh0);
  not not_437 (not_437_out, bh1);
  not not_438 (not_438_out, sh0);
  not not_439 (not_439_out, sh1);
  not not_440 (not_440_out, bh0);
  not not_441 (not_441_out, bh1);
  not not_442 (not_442_out, bh0);
  not not_443 (not_443_out, bh1);
  not not_444 (not_444_out, sh0);
  not not_445 (not_445_out, sh1);
  not not_446 (not_446_out, bh0);
  not not_447 (not_447_out, bh1);
  not not_448 (not_448_out, bh0);
  not not_449 (not_449_out, bh2);
  not not_450 (not_450_out, bh3);
  not not_451 (not_451_out, bh4);
  not not_452 (not_452_out, sh0);
  not not_453 (not_453_out, sh1);
  not not_454 (not_454_out, bh0);
  not not_455 (not_455_out, bh2);
  not not_456 (not_456_out, bh3);
  not not_457 (not_457_out, sh0);
  not not_458 (not_458_out, sh1);
  not not_459 (not_459_out, sh3);
  not not_460 (not_460_out, bh0);
  not not_461 (not_461_out, bh2);
  not not_462 (not_462_out, bh3);
  not not_463 (not_463_out, sh0);
  not not_464 (not_464_out, sh1);
  not not_465 (not_465_out, sh4);
  not not_466 (not_466_out, bh0);
  not not_467 (not_467_out, bh2);
  not not_468 (not_468_out, bh4);
  not not_469 (not_469_out, sh0);
  not not_470 (not_470_out, sh1);
  not not_471 (not_471_out, sh3);
  not not_472 (not_472_out, bh0);
  not not_473 (not_473_out, bh2);
  not not_474 (not_474_out, sh0);
  not not_475 (not_475_out, sh1);
  not not_476 (not_476_out, sh2);
  not not_477 (not_477_out, bh0);
  not not_478 (not_478_out, bh2);
  not not_479 (not_479_out, sh0);
  not not_480 (not_480_out, sh1);
  not not_481 (not_481_out, sh3);
  not not_482 (not_482_out, sh4);
  not not_483 (not_483_out, bh0);
  not not_484 (not_484_out, bh3);
  not not_485 (not_485_out, bh4);
  not not_486 (not_486_out, sh0);
  not not_487 (not_487_out, sh1);
  not not_488 (not_488_out, sh2);
  not not_489 (not_489_out, bh0);
  not not_490 (not_490_out, bh3);
  not not_491 (not_491_out, sh0);
  not not_492 (not_492_out, sh1);
  not not_493 (not_493_out, sh2);
  not not_494 (not_494_out, sh3);
  not not_495 (not_495_out, bh0);
  not not_496 (not_496_out, bh3);
  not not_497 (not_497_out, sh0);
  not not_498 (not_498_out, sh1);
  not not_499 (not_499_out, sh2);
  not not_500 (not_500_out, sh4);
  not not_501 (not_501_out, bh0);
  not not_502 (not_502_out, bh4);
  not not_503 (not_503_out, sh0);
  not not_504 (not_504_out, sh1);
  not not_505 (not_505_out, sh2);
  not not_506 (not_506_out, sh3);
  not not_507 (not_507_out, bh0);
  not not_508 (not_508_out, sh0);
  not not_509 (not_509_out, sh1);
  not not_510 (not_510_out, sh2);
  not not_511 (not_511_out, sh3);
  not not_512 (not_512_out, sh4);
  not not_513 (not_513_out, bh0);
  not not_514 (not_514_out, bh2);
  not not_515 (not_515_out, bh3);
  not not_516 (not_516_out, bh4);
  not not_517 (not_517_out, bh0);
  not not_518 (not_518_out, bh2);
  not not_519 (not_519_out, bh3);
  not not_520 (not_520_out, sh3);
  not not_521 (not_521_out, bh0);
  not not_522 (not_522_out, bh2);
  not not_523 (not_523_out, bh3);
  not not_524 (not_524_out, sh4);
  not not_525 (not_525_out, bh0);
  not not_526 (not_526_out, bh2);
  not not_527 (not_527_out, bh4);
  not not_528 (not_528_out, sh3);
  not not_529 (not_529_out, bh0);
  not not_530 (not_530_out, bh2);
  not not_531 (not_531_out, sh2);
  not not_532 (not_532_out, bh0);
  not not_533 (not_533_out, bh2);
  not not_534 (not_534_out, sh3);
  not not_535 (not_535_out, sh4);
  not not_536 (not_536_out, bh0);
  not not_537 (not_537_out, bh3);
  not not_538 (not_538_out, bh4);
  not not_539 (not_539_out, sh2);
  not not_540 (not_540_out, bh0);
  not not_541 (not_541_out, bh3);
  not not_542 (not_542_out, sh2);
  not not_543 (not_543_out, sh3);
  not not_544 (not_544_out, bh0);
  not not_545 (not_545_out, bh3);
  not not_546 (not_546_out, sh2);
  not not_547 (not_547_out, sh4);
  not not_548 (not_548_out, bh0);
  not not_549 (not_549_out, bh4);
  not not_550 (not_550_out, sh2);
  not not_551 (not_551_out, sh3);
  not not_552 (not_552_out, bh0);
  not not_553 (not_553_out, sh2);
  not not_554 (not_554_out, sh3);
  not not_555 (not_555_out, sh4);
  not not_556 (not_556_out, bh0);
  not not_557 (not_557_out, sh1);
  not not_558 (not_558_out, bh0);
  not not_559 (not_559_out, sh1);
  not not_560 (not_560_out, bh0);
  not not_561 (not_561_out, sh1);
  not not_562 (not_562_out, bh0);
  not not_563 (not_563_out, sh1);
  not not_564 (not_564_out, bh0);
  not not_565 (not_565_out, sh1);
  not not_566 (not_566_out, bh0);
  not not_567 (not_567_out, sh1);
  not not_568 (not_568_out, bh0);
  not not_569 (not_569_out, sh1);
  not not_570 (not_570_out, bh1);
  not not_571 (not_571_out, bh2);
  not not_572 (not_572_out, bh3);
  not not_573 (not_573_out, bh4);
  not not_574 (not_574_out, sh1);
  not not_575 (not_575_out, bh1);
  not not_576 (not_576_out, bh2);
  not not_577 (not_577_out, bh3);
  not not_578 (not_578_out, sh1);
  not not_579 (not_579_out, sh3);
  not not_580 (not_580_out, bh1);
  not not_581 (not_581_out, bh2);
  not not_582 (not_582_out, bh3);
  not not_583 (not_583_out, sh1);
  not not_584 (not_584_out, sh4);
  not not_585 (not_585_out, bh1);
  not not_586 (not_586_out, bh2);
  not not_587 (not_587_out, bh4);
  not not_588 (not_588_out, sh1);
  not not_589 (not_589_out, sh3);
  not not_590 (not_590_out, bh1);
  not not_591 (not_591_out, bh2);
  not not_592 (not_592_out, sh1);
  not not_593 (not_593_out, sh2);
  not not_594 (not_594_out, bh1);
  not not_595 (not_595_out, bh2);
  not not_596 (not_596_out, sh1);
  not not_597 (not_597_out, sh3);
  not not_598 (not_598_out, sh4);
  not not_599 (not_599_out, bh1);
  not not_600 (not_600_out, bh3);
  not not_601 (not_601_out, bh4);
  not not_602 (not_602_out, sh1);
  not not_603 (not_603_out, sh2);
  not not_604 (not_604_out, bh1);
  not not_605 (not_605_out, bh3);
  not not_606 (not_606_out, sh1);
  not not_607 (not_607_out, sh2);
  not not_608 (not_608_out, sh3);
  not not_609 (not_609_out, bh1);
  not not_610 (not_610_out, bh3);
  not not_611 (not_611_out, sh1);
  not not_612 (not_612_out, sh2);
  not not_613 (not_613_out, sh4);
  not not_614 (not_614_out, bh1);
  not not_615 (not_615_out, bh4);
  not not_616 (not_616_out, sh1);
  not not_617 (not_617_out, sh2);
  not not_618 (not_618_out, sh3);
  not not_619 (not_619_out, bh1);
  not not_620 (not_620_out, sh1);
  not not_621 (not_621_out, sh2);
  not not_622 (not_622_out, sh3);
  not not_623 (not_623_out, sh4);
  not not_624 (not_624_out, bh1);
  not not_625 (not_625_out, sh0);
  not not_626 (not_626_out, bh1);
  not not_627 (not_627_out, sh0);
  not not_628 (not_628_out, bh1);
  not not_629 (not_629_out, sh0);
  not not_630 (not_630_out, bh1);
  not not_631 (not_631_out, sh0);
  not not_632 (not_632_out, bh1);
  not not_633 (not_633_out, sh0);
  not not_634 (not_634_out, bh1);
  not not_635 (not_635_out, sh0);
  not not_636 (not_636_out, bh1);
  not not_637 (not_637_out, sh0);
  not not_638 (not_638_out, bh2);
  not not_639 (not_639_out, bh3);
  not not_640 (not_640_out, bh4);
  not not_641 (not_641_out, sh0);
  not not_642 (not_642_out, bh2);
  not not_643 (not_643_out, bh3);
  not not_644 (not_644_out, sh0);
  not not_645 (not_645_out, sh3);
  not not_646 (not_646_out, bh2);
  not not_647 (not_647_out, bh3);
  not not_648 (not_648_out, sh0);
  not not_649 (not_649_out, sh4);
  not not_650 (not_650_out, bh2);
  not not_651 (not_651_out, bh4);
  not not_652 (not_652_out, sh0);
  not not_653 (not_653_out, sh3);
  not not_654 (not_654_out, bh2);
  not not_655 (not_655_out, sh0);
  not not_656 (not_656_out, sh2);
  not not_657 (not_657_out, bh2);
  not not_658 (not_658_out, sh0);
  not not_659 (not_659_out, sh3);
  not not_660 (not_660_out, sh4);
  not not_661 (not_661_out, bh3);
  not not_662 (not_662_out, bh4);
  not not_663 (not_663_out, sh0);
  not not_664 (not_664_out, sh2);
  not not_665 (not_665_out, bh3);
  not not_666 (not_666_out, sh0);
  not not_667 (not_667_out, sh2);
  not not_668 (not_668_out, sh3);
  not not_669 (not_669_out, bh3);
  not not_670 (not_670_out, sh0);
  not not_671 (not_671_out, sh2);
  not not_672 (not_672_out, sh4);
  not not_673 (not_673_out, bh4);
  not not_674 (not_674_out, sh0);
  not not_675 (not_675_out, sh2);
  not not_676 (not_676_out, sh3);
  not not_677 (not_677_out, sh0);
  not not_678 (not_678_out, sh2);
  not not_679 (not_679_out, sh3);
  not not_680 (not_680_out, sh4);
  not not_681 (not_681_out, sh0);
  not not_682 (not_682_out, sh1);
  not not_683 (not_683_out, sh0);
  not not_684 (not_684_out, sh1);
  not not_685 (not_685_out, sh0);
  not not_686 (not_686_out, sh1);
  not not_687 (not_687_out, sh0);
  not not_688 (not_688_out, sh1);
  not not_689 (not_689_out, sh0);
  not not_690 (not_690_out, sh1);
  not not_691 (not_691_out, sh0);
  not not_692 (not_692_out, sh1);
  not not_693 (not_693_out, sh0);
  not not_694 (not_694_out, sh1);
  not not_695 (not_695_out, bh2);
  not not_696 (not_696_out, bh3);
  not not_697 (not_697_out, bh4);
  not not_698 (not_698_out, bh2);
  not not_699 (not_699_out, bh3);
  not not_700 (not_700_out, sh3);
  not not_701 (not_701_out, bh2);
  not not_702 (not_702_out, bh3);
  not not_703 (not_703_out, sh4);
  not not_704 (not_704_out, bh2);
  not not_705 (not_705_out, bh4);
  not not_706 (not_706_out, sh3);
  not not_707 (not_707_out, bh2);
  not not_708 (not_708_out, sh3);
  not not_709 (not_709_out, sh4);
  not not_710 (not_710_out, bh2);
  not not_711 (not_711_out, sh2);
  not not_712 (not_712_out, bh2);
  not not_713 (not_713_out, sh2);
  not not_714 (not_714_out, bh2);
  not not_715 (not_715_out, sh2);
  not not_716 (not_716_out, bh3);
  not not_717 (not_717_out, bh4);
  not not_718 (not_718_out, sh2);
  not not_719 (not_719_out, bh3);
  not not_720 (not_720_out, sh2);
  not not_721 (not_721_out, sh3);
  not not_722 (not_722_out, bh3);
  not not_723 (not_723_out, sh2);
  not not_724 (not_724_out, sh4);
  not not_725 (not_725_out, bh4);
  not not_726 (not_726_out, sh2);
  not not_727 (not_727_out, sh3);
  not not_728 (not_728_out, sh2);
  not not_729 (not_729_out, sh3);
  not not_730 (not_730_out, sh4);
  not not_731 (not_731_out, bh3);
  not not_732 (not_732_out, bh4);
  not not_733 (not_733_out, bh3);
  not not_734 (not_734_out, sh4);
  not not_735 (not_735_out, bh3);
  not not_736 (not_736_out, sh3);
  not not_737 (not_737_out, bh4);
  not not_738 (not_738_out, sh3);
  not not_739 (not_739_out, sh3);
  not not_740 (not_740_out, sh4);
  not not_741 (not_741_out, bh4);
  not not_742 (not_742_out, sh4);
  and and_1 (and_1_out, not_1_out, not_2_out, not_3_out, not_4_out, not_5_out, sh0, not_6_out);
  and and_2 (and_2_out, not_7_out, not_8_out, not_9_out, not_10_out, sh0, not_11_out, not_12_out);
  and and_3 (and_3_out, not_13_out, not_14_out, not_15_out, not_16_out, sh0, not_17_out, not_18_out);
  and and_4 (and_4_out, not_19_out, not_20_out, not_21_out, not_22_out, sh0, not_23_out, not_24_out);
  and and_5 (and_5_out, not_25_out, not_26_out, not_27_out, sh0, not_28_out, not_29_out);
  and and_6 (and_6_out, not_30_out, not_31_out, not_32_out, sh0, not_33_out, not_34_out, not_35_out);
  and and_7 (and_7_out, not_36_out, not_37_out, not_38_out, not_39_out, sh0, not_40_out, not_41_out);
  and and_8 (and_8_out, not_42_out, not_43_out, not_44_out, sh0, not_45_out, not_46_out, not_47_out);
  and and_9 (and_9_out, not_48_out, not_49_out, not_50_out, sh0, not_51_out, not_52_out, not_53_out);
  and and_10 (and_10_out, not_54_out, not_55_out, not_56_out, sh0, not_57_out, not_58_out, not_59_out);
  and and_11 (and_11_out, not_60_out, not_61_out, sh0, not_62_out, not_63_out, not_64_out, not_65_out);
  and and_12 (and_12_out, not_66_out, not_67_out, bh4, not_68_out, sh1, sh2, sh3, sh4);
  and and_13 (and_13_out, not_69_out, not_70_out, bh3, not_71_out, sh1, sh2, sh3);
  and and_14 (and_14_out, not_72_out, not_73_out, bh3, bh4, not_74_out, sh1, sh2, sh4);
  and and_15 (and_15_out, not_75_out, not_76_out, bh2, not_77_out, sh1, sh2);
  and and_16 (and_16_out, not_78_out, not_79_out, bh2, bh4, not_80_out, sh1, sh3, sh4);
  and and_17 (and_17_out, not_81_out, not_82_out, bh2, bh3, not_83_out, sh1, sh3);
  and and_18 (and_18_out, not_84_out, not_85_out, bh2, bh3, bh4, not_86_out, sh1, sh4);
  and and_19 (and_19_out, not_87_out, bh1, not_88_out, not_89_out, not_90_out, not_91_out, sh1);
  and and_20 (and_20_out, not_92_out, bh1, not_93_out, not_94_out, not_95_out, sh1, not_96_out);
  and and_21 (and_21_out, not_97_out, bh1, not_98_out, not_99_out, not_100_out, sh1, not_101_out);
  and and_22 (and_22_out, not_102_out, bh1, not_103_out, not_104_out, not_105_out, sh1, not_106_out);
  and and_23 (and_23_out, not_107_out, bh1, not_108_out, not_109_out, sh1, not_110_out);
  and and_24 (and_24_out, not_111_out, bh1, not_112_out, not_113_out, sh1, not_114_out, not_115_out);
  and and_25 (and_25_out, not_116_out, bh1, not_117_out, not_118_out, not_119_out, sh1, not_120_out);
  and and_26 (and_26_out, not_121_out, bh1, not_122_out, not_123_out, sh1, not_124_out, not_125_out);
  and and_27 (and_27_out, not_126_out, bh1, not_127_out, not_128_out, sh1, not_129_out, not_130_out);
  and and_28 (and_28_out, not_131_out, bh1, not_132_out, not_133_out, sh1, not_134_out, not_135_out);
  and and_29 (and_29_out, not_136_out, bh1, not_137_out, sh1, not_138_out, not_139_out, not_140_out);
  and and_30 (and_30_out, not_141_out, bh1, bh4, not_142_out, not_143_out, sh2, sh3, sh4);
  and and_31 (and_31_out, not_144_out, bh1, bh4, sh0, sh1, sh2, sh3, sh4);
  and and_32 (and_32_out, not_145_out, bh1, bh3, not_146_out, not_147_out, sh2, sh3);
  and and_33 (and_33_out, not_148_out, bh1, bh3, sh0, sh1, sh2, sh3);
  and and_34 (and_34_out, not_149_out, bh1, bh3, bh4, not_150_out, not_151_out, sh2, sh4);
  and and_35 (and_35_out, not_152_out, bh1, bh3, bh4, sh0, sh1, sh2, sh4);
  and and_36 (and_36_out, not_153_out, bh1, bh2, not_154_out, not_155_out, sh2);
  and and_37 (and_37_out, not_156_out, bh1, bh2, sh0, sh1, sh2);
  and and_38 (and_38_out, not_157_out, bh1, bh2, bh4, not_158_out, not_159_out, sh3, sh4);
  and and_39 (and_39_out, not_160_out, bh1, bh2, bh4, sh0, sh1, sh3, sh4);
  and and_40 (and_40_out, not_161_out, bh1, bh2, bh3, not_162_out, not_163_out, sh3);
  and and_41 (and_41_out, not_164_out, bh1, bh2, bh3, sh0, sh1, sh3);
  and and_42 (and_42_out, not_165_out, bh1, bh2, bh3, bh4, not_166_out, not_167_out, sh4);
  and and_43 (and_43_out, not_168_out, bh1, bh2, bh3, bh4, sh0, sh1, sh4);
  and and_44 (and_44_out, bh0, not_169_out, not_170_out, not_171_out, not_172_out, not_173_out, not_174_out);
  and and_45 (and_45_out, bh0, not_175_out, not_176_out, not_177_out, not_178_out, not_179_out, not_180_out);
  and and_46 (and_46_out, bh0, not_181_out, not_182_out, not_183_out, not_184_out, not_185_out, not_186_out);
  and and_47 (and_47_out, bh0, not_187_out, not_188_out, not_189_out, not_190_out, not_191_out, not_192_out);
  and and_48 (and_48_out, bh0, not_193_out, not_194_out, not_195_out, not_196_out, not_197_out);
  and and_49 (and_49_out, bh0, not_198_out, not_199_out, not_200_out, not_201_out, not_202_out, not_203_out);
  and and_50 (and_50_out, bh0, not_204_out, not_205_out, not_206_out, not_207_out, not_208_out, not_209_out);
  and and_51 (and_51_out, bh0, not_210_out, not_211_out, not_212_out, not_213_out, not_214_out, not_215_out);
  and and_52 (and_52_out, bh0, not_216_out, not_217_out, not_218_out, not_219_out, not_220_out, not_221_out);
  and and_53 (and_53_out, bh0, not_222_out, not_223_out, not_224_out, not_225_out, not_226_out, not_227_out);
  and and_54 (and_54_out, bh0, not_228_out, not_229_out, not_230_out, not_231_out, not_232_out, not_233_out);
  and and_55 (and_55_out, bh0, not_234_out, not_235_out, not_236_out, not_237_out, sh0, sh1);
  and and_56 (and_56_out, bh0, not_238_out, not_239_out, not_240_out, sh0, sh1, not_241_out);
  and and_57 (and_57_out, bh0, not_242_out, not_243_out, not_244_out, sh0, sh1, not_245_out);
  and and_58 (and_58_out, bh0, not_246_out, not_247_out, not_248_out, sh0, sh1, not_249_out);
  and and_59 (and_59_out, bh0, not_250_out, not_251_out, sh0, sh1, not_252_out);
  and and_60 (and_60_out, bh0, not_253_out, not_254_out, sh0, sh1, not_255_out, not_256_out);
  and and_61 (and_61_out, bh0, not_257_out, not_258_out, not_259_out, sh0, sh1, not_260_out);
  and and_62 (and_62_out, bh0, not_261_out, not_262_out, sh0, sh1, not_263_out, not_264_out);
  and and_63 (and_63_out, bh0, not_265_out, not_266_out, sh0, sh1, not_267_out, not_268_out);
  and and_64 (and_64_out, bh0, not_269_out, not_270_out, sh0, sh1, not_271_out, not_272_out);
  and and_65 (and_65_out, bh0, not_273_out, sh0, sh1, not_274_out, not_275_out, not_276_out);
  and and_66 (and_66_out, bh0, not_277_out, bh4, sh0, not_278_out, sh2, sh3, sh4);
  and and_67 (and_67_out, bh0, not_279_out, bh3, sh0, not_280_out, sh2, sh3);
  and and_68 (and_68_out, bh0, not_281_out, bh3, bh4, sh0, not_282_out, sh2, sh4);
  and and_69 (and_69_out, bh0, not_283_out, bh2, sh0, not_284_out, sh2);
  and and_70 (and_70_out, bh0, not_285_out, bh2, bh4, sh0, not_286_out, sh3, sh4);
  and and_71 (and_71_out, bh0, not_287_out, bh2, bh3, sh0, not_288_out, sh3);
  and and_72 (and_72_out, bh0, not_289_out, bh2, bh3, bh4, sh0, not_290_out, sh4);
  and and_73 (and_73_out, bh0, bh1, not_291_out, not_292_out, not_293_out, sh0, not_294_out);
  and and_74 (and_74_out, bh0, bh1, not_295_out, not_296_out, sh0, not_297_out, not_298_out);
  and and_75 (and_75_out, bh0, bh1, not_299_out, not_300_out, sh0, not_301_out, not_302_out);
  and and_76 (and_76_out, bh0, bh1, not_303_out, not_304_out, sh0, not_305_out, not_306_out);
  and and_77 (and_77_out, bh0, bh1, not_307_out, sh0, not_308_out, not_309_out);
  and and_78 (and_78_out, bh0, bh1, not_310_out, sh0, not_311_out, not_312_out, not_313_out);
  and and_79 (and_79_out, bh0, bh1, not_314_out, not_315_out, sh0, not_316_out, not_317_out);
  and and_80 (and_80_out, bh0, bh1, not_318_out, sh0, not_319_out, not_320_out, not_321_out);
  and and_81 (and_81_out, bh0, bh1, not_322_out, sh0, not_323_out, not_324_out, not_325_out);
  and and_82 (and_82_out, bh0, bh1, not_326_out, sh0, not_327_out, not_328_out, not_329_out);
  and and_83 (and_83_out, bh0, bh1, sh0, not_330_out, not_331_out, not_332_out, not_333_out);
  and and_84 (and_84_out, bh0, bh1, bh4, not_334_out, sh1, sh2, sh3, sh4);
  and and_85 (and_85_out, bh0, bh1, bh3, not_335_out, sh1, sh2, sh3);
  and and_86 (and_86_out, bh0, bh1, bh3, bh4, not_336_out, sh1, sh2, sh4);
  and and_87 (and_87_out, bh0, bh1, bh2, not_337_out, sh1, sh2);
  and and_88 (and_88_out, bh0, bh1, bh2, bh4, not_338_out, sh1, sh3, sh4);
  and and_89 (and_89_out, bh0, bh1, bh2, bh3, not_339_out, sh1, sh3);
  and and_90 (and_90_out, bh0, bh1, bh2, bh3, bh4, not_340_out, sh1, sh4);
  and and_91 (and_91_out, not_341_out, not_342_out, not_343_out, not_344_out, not_345_out, not_346_out, sh1);
  and and_92 (and_92_out, not_347_out, not_348_out, not_349_out, not_350_out, not_351_out, sh1, not_352_out);
  and and_93 (and_93_out, not_353_out, not_354_out, not_355_out, not_356_out, not_357_out, sh1, not_358_out);
  and and_94 (and_94_out, not_359_out, not_360_out, not_361_out, not_362_out, not_363_out, sh1, not_364_out);
  and and_95 (and_95_out, not_365_out, not_366_out, not_367_out, not_368_out, sh1, not_369_out);
  and and_96 (and_96_out, not_370_out, not_371_out, not_372_out, not_373_out, sh1, not_374_out, not_375_out);
  and and_97 (and_97_out, not_376_out, not_377_out, not_378_out, not_379_out, not_380_out, sh1, not_381_out);
  and and_98 (and_98_out, not_382_out, not_383_out, not_384_out, not_385_out, sh1, not_386_out, not_387_out);
  and and_99 (and_99_out, not_388_out, not_389_out, not_390_out, not_391_out, sh1, not_392_out, not_393_out);
  and and_100 (and_100_out, not_394_out, not_395_out, not_396_out, not_397_out, sh1, not_398_out, not_399_out);
  and and_101 (and_101_out, not_400_out, not_401_out, not_402_out, sh1, not_403_out, not_404_out, not_405_out);
  and and_102 (and_102_out, not_406_out, not_407_out, bh4, not_408_out, not_409_out, sh2, sh3, sh4);
  and and_103 (and_103_out, not_410_out, not_411_out, bh4, sh0, sh1, sh2, sh3, sh4);
  and and_104 (and_104_out, not_412_out, not_413_out, bh3, not_414_out, not_415_out, sh2, sh3);
  and and_105 (and_105_out, not_416_out, not_417_out, bh3, sh0, sh1, sh2, sh3);
  and and_106 (and_106_out, not_418_out, not_419_out, bh3, bh4, not_420_out, not_421_out, sh2, sh4);
  and and_107 (and_107_out, not_422_out, not_423_out, bh3, bh4, sh0, sh1, sh2, sh4);
  and and_108 (and_108_out, not_424_out, not_425_out, bh2, not_426_out, not_427_out, sh2);
  and and_109 (and_109_out, not_428_out, not_429_out, bh2, sh0, sh1, sh2);
  and and_110 (and_110_out, not_430_out, not_431_out, bh2, bh4, not_432_out, not_433_out, sh3, sh4);
  and and_111 (and_111_out, not_434_out, not_435_out, bh2, bh4, sh0, sh1, sh3, sh4);
  and and_112 (and_112_out, not_436_out, not_437_out, bh2, bh3, not_438_out, not_439_out, sh3);
  and and_113 (and_113_out, not_440_out, not_441_out, bh2, bh3, sh0, sh1, sh3);
  and and_114 (and_114_out, not_442_out, not_443_out, bh2, bh3, bh4, not_444_out, not_445_out, sh4);
  and and_115 (and_115_out, not_446_out, not_447_out, bh2, bh3, bh4, sh0, sh1, sh4);
  and and_116 (and_116_out, not_448_out, bh1, not_449_out, not_450_out, not_451_out, not_452_out, not_453_out);
  and and_117 (and_117_out, not_454_out, bh1, not_455_out, not_456_out, not_457_out, not_458_out, not_459_out);
  and and_118 (and_118_out, not_460_out, bh1, not_461_out, not_462_out, not_463_out, not_464_out, not_465_out);
  and and_119 (and_119_out, not_466_out, bh1, not_467_out, not_468_out, not_469_out, not_470_out, not_471_out);
  and and_120 (and_120_out, not_472_out, bh1, not_473_out, not_474_out, not_475_out, not_476_out);
  and and_121 (and_121_out, not_477_out, bh1, not_478_out, not_479_out, not_480_out, not_481_out, not_482_out);
  and and_122 (and_122_out, not_483_out, bh1, not_484_out, not_485_out, not_486_out, not_487_out, not_488_out);
  and and_123 (and_123_out, not_489_out, bh1, not_490_out, not_491_out, not_492_out, not_493_out, not_494_out);
  and and_124 (and_124_out, not_495_out, bh1, not_496_out, not_497_out, not_498_out, not_499_out, not_500_out);
  and and_125 (and_125_out, not_501_out, bh1, not_502_out, not_503_out, not_504_out, not_505_out, not_506_out);
  and and_126 (and_126_out, not_507_out, bh1, not_508_out, not_509_out, not_510_out, not_511_out, not_512_out);
  and and_127 (and_127_out, not_513_out, bh1, not_514_out, not_515_out, not_516_out, sh0, sh1);
  and and_128 (and_128_out, not_517_out, bh1, not_518_out, not_519_out, sh0, sh1, not_520_out);
  and and_129 (and_129_out, not_521_out, bh1, not_522_out, not_523_out, sh0, sh1, not_524_out);
  and and_130 (and_130_out, not_525_out, bh1, not_526_out, not_527_out, sh0, sh1, not_528_out);
  and and_131 (and_131_out, not_529_out, bh1, not_530_out, sh0, sh1, not_531_out);
  and and_132 (and_132_out, not_532_out, bh1, not_533_out, sh0, sh1, not_534_out, not_535_out);
  and and_133 (and_133_out, not_536_out, bh1, not_537_out, not_538_out, sh0, sh1, not_539_out);
  and and_134 (and_134_out, not_540_out, bh1, not_541_out, sh0, sh1, not_542_out, not_543_out);
  and and_135 (and_135_out, not_544_out, bh1, not_545_out, sh0, sh1, not_546_out, not_547_out);
  and and_136 (and_136_out, not_548_out, bh1, not_549_out, sh0, sh1, not_550_out, not_551_out);
  and and_137 (and_137_out, not_552_out, bh1, sh0, sh1, not_553_out, not_554_out, not_555_out);
  and and_138 (and_138_out, not_556_out, bh1, bh4, sh0, not_557_out, sh2, sh3, sh4);
  and and_139 (and_139_out, not_558_out, bh1, bh3, sh0, not_559_out, sh2, sh3);
  and and_140 (and_140_out, not_560_out, bh1, bh3, bh4, sh0, not_561_out, sh2, sh4);
  and and_141 (and_141_out, not_562_out, bh1, bh2, sh0, not_563_out, sh2);
  and and_142 (and_142_out, not_564_out, bh1, bh2, bh4, sh0, not_565_out, sh3, sh4);
  and and_143 (and_143_out, not_566_out, bh1, bh2, bh3, sh0, not_567_out, sh3);
  and and_144 (and_144_out, not_568_out, bh1, bh2, bh3, bh4, sh0, not_569_out, sh4);
  and and_145 (and_145_out, bh0, not_570_out, not_571_out, not_572_out, not_573_out, sh0, not_574_out);
  and and_146 (and_146_out, bh0, not_575_out, not_576_out, not_577_out, sh0, not_578_out, not_579_out);
  and and_147 (and_147_out, bh0, not_580_out, not_581_out, not_582_out, sh0, not_583_out, not_584_out);
  and and_148 (and_148_out, bh0, not_585_out, not_586_out, not_587_out, sh0, not_588_out, not_589_out);
  and and_149 (and_149_out, bh0, not_590_out, not_591_out, sh0, not_592_out, not_593_out);
  and and_150 (and_150_out, bh0, not_594_out, not_595_out, sh0, not_596_out, not_597_out, not_598_out);
  and and_151 (and_151_out, bh0, not_599_out, not_600_out, not_601_out, sh0, not_602_out, not_603_out);
  and and_152 (and_152_out, bh0, not_604_out, not_605_out, sh0, not_606_out, not_607_out, not_608_out);
  and and_153 (and_153_out, bh0, not_609_out, not_610_out, sh0, not_611_out, not_612_out, not_613_out);
  and and_154 (and_154_out, bh0, not_614_out, not_615_out, sh0, not_616_out, not_617_out, not_618_out);
  and and_155 (and_155_out, bh0, not_619_out, sh0, not_620_out, not_621_out, not_622_out, not_623_out);
  and and_156 (and_156_out, bh0, not_624_out, bh4, not_625_out, sh1, sh2, sh3, sh4);
  and and_157 (and_157_out, bh0, not_626_out, bh3, not_627_out, sh1, sh2, sh3);
  and and_158 (and_158_out, bh0, not_628_out, bh3, bh4, not_629_out, sh1, sh2, sh4);
  and and_159 (and_159_out, bh0, not_630_out, bh2, not_631_out, sh1, sh2);
  and and_160 (and_160_out, bh0, not_632_out, bh2, bh4, not_633_out, sh1, sh3, sh4);
  and and_161 (and_161_out, bh0, not_634_out, bh2, bh3, not_635_out, sh1, sh3);
  and and_162 (and_162_out, bh0, not_636_out, bh2, bh3, bh4, not_637_out, sh1, sh4);
  and and_163 (and_163_out, bh0, bh1, not_638_out, not_639_out, not_640_out, not_641_out, sh1);
  and and_164 (and_164_out, bh0, bh1, not_642_out, not_643_out, not_644_out, sh1, not_645_out);
  and and_165 (and_165_out, bh0, bh1, not_646_out, not_647_out, not_648_out, sh1, not_649_out);
  and and_166 (and_166_out, bh0, bh1, not_650_out, not_651_out, not_652_out, sh1, not_653_out);
  and and_167 (and_167_out, bh0, bh1, not_654_out, not_655_out, sh1, not_656_out);
  and and_168 (and_168_out, bh0, bh1, not_657_out, not_658_out, sh1, not_659_out, not_660_out);
  and and_169 (and_169_out, bh0, bh1, not_661_out, not_662_out, not_663_out, sh1, not_664_out);
  and and_170 (and_170_out, bh0, bh1, not_665_out, not_666_out, sh1, not_667_out, not_668_out);
  and and_171 (and_171_out, bh0, bh1, not_669_out, not_670_out, sh1, not_671_out, not_672_out);
  and and_172 (and_172_out, bh0, bh1, not_673_out, not_674_out, sh1, not_675_out, not_676_out);
  and and_173 (and_173_out, bh0, bh1, not_677_out, sh1, not_678_out, not_679_out, not_680_out);
  and and_174 (and_174_out, bh0, bh1, bh4, not_681_out, not_682_out, sh2, sh3, sh4);
  and and_175 (and_175_out, bh0, bh1, bh4, sh0, sh1, sh2, sh3, sh4);
  and and_176 (and_176_out, bh0, bh1, bh3, not_683_out, not_684_out, sh2, sh3);
  and and_177 (and_177_out, bh0, bh1, bh3, sh0, sh1, sh2, sh3);
  and and_178 (and_178_out, bh0, bh1, bh3, bh4, not_685_out, not_686_out, sh2, sh4);
  and and_179 (and_179_out, bh0, bh1, bh3, bh4, sh0, sh1, sh2, sh4);
  and and_180 (and_180_out, bh0, bh1, bh2, not_687_out, not_688_out, sh2);
  and and_181 (and_181_out, bh0, bh1, bh2, sh0, sh1, sh2);
  and and_182 (and_182_out, bh0, bh1, bh2, bh4, not_689_out, not_690_out, sh3, sh4);
  and and_183 (and_183_out, bh0, bh1, bh2, bh4, sh0, sh1, sh3, sh4);
  and and_184 (and_184_out, bh0, bh1, bh2, bh3, not_691_out, not_692_out, sh3);
  and and_185 (and_185_out, bh0, bh1, bh2, bh3, sh0, sh1, sh3);
  and and_186 (and_186_out, bh0, bh1, bh2, bh3, bh4, not_693_out, not_694_out, sh4);
  and and_187 (and_187_out, bh0, bh1, bh2, bh3, bh4, sh0, sh1, sh4);
  and and_188 (and_188_out, not_695_out, not_696_out, not_697_out, sh2);
  and and_189 (and_189_out, not_698_out, not_699_out, sh2, not_700_out);
  and and_190 (and_190_out, not_701_out, not_702_out, sh2, not_703_out);
  and and_191 (and_191_out, not_704_out, not_705_out, sh2, not_706_out);
  and and_192 (and_192_out, not_707_out, sh2, not_708_out, not_709_out);
  and and_193 (and_193_out, not_710_out, bh4, not_711_out, sh3, sh4);
  and and_194 (and_194_out, not_712_out, bh3, not_713_out, sh3);
  and and_195 (and_195_out, not_714_out, bh3, bh4, not_715_out, sh4);
  and and_196 (and_196_out, bh2, not_716_out, not_717_out, not_718_out);
  and and_197 (and_197_out, bh2, not_719_out, not_720_out, not_721_out);
  and and_198 (and_198_out, bh2, not_722_out, not_723_out, not_724_out);
  and and_199 (and_199_out, bh2, not_725_out, not_726_out, not_727_out);
  and and_200 (and_200_out, bh2, not_728_out, not_729_out, not_730_out);
  and and_201 (and_201_out, bh2, bh4, sh2, sh3, sh4);
  and and_202 (and_202_out, bh2, bh3, sh2, sh3);
  and and_203 (and_203_out, bh2, bh3, bh4, sh2, sh4);
  and and_204 (and_204_out, not_731_out, not_732_out, sh3);
  and and_205 (and_205_out, not_733_out, sh3, not_734_out);
  and and_206 (and_206_out, not_735_out, bh4, not_736_out, sh4);
  and and_207 (and_207_out, bh3, not_737_out, not_738_out);
  and and_208 (and_208_out, bh3, not_739_out, not_740_out);
  and and_209 (and_209_out, bh3, bh4, sh3, sh4);
  and and_210 (and_210_out, not_741_out, sh4);
  or or_1 (h4, and_210_out, and_211_out);
  and and_211 (and_211_out, bh4, not_742_out);
  or or_2 (h2, and_188_out, and_189_out, and_190_out, and_191_out, and_192_out, and_193_out, and_194_out, and_195_out, and_196_out, and_197_out, and_198_out, and_199_out, and_200_out, and_201_out, and_202_out, and_203_out);
  or or_3 (h3, and_204_out, and_205_out, and_206_out, and_207_out, and_208_out, and_209_out);
  or or_4 (or_4_out, and_91_out, and_92_out, and_93_out, and_94_out, and_95_out, and_96_out, and_97_out, and_98_out, and_99_out, and_100_out, and_101_out, and_102_out, and_103_out, and_104_out, and_105_out, and_106_out, and_107_out, and_108_out, and_109_out, and_110_out, and_111_out, and_112_out, and_113_out, and_114_out, and_115_out);
  or or_5 (or_5_out, and_116_out, and_117_out, and_118_out, and_119_out, and_120_out, and_121_out, and_122_out, and_123_out, and_124_out, and_125_out, and_126_out, and_127_out, and_128_out, and_129_out, and_130_out, and_131_out, and_132_out, and_133_out, and_134_out, and_135_out, and_136_out, and_137_out, and_138_out, and_139_out);
  or or_6 (or_6_out, and_140_out, and_141_out, and_142_out, and_143_out, and_144_out, and_145_out, and_146_out, and_147_out, and_148_out, and_149_out, and_150_out, and_151_out, and_152_out, and_153_out, and_154_out, and_155_out, and_156_out, and_157_out, and_158_out, and_159_out, and_160_out, and_161_out, and_162_out, and_163_out);
  or or_7 (or_7_out, and_164_out, and_165_out, and_166_out, and_167_out, and_168_out, and_169_out, and_170_out, and_171_out, and_172_out, and_173_out, and_174_out, and_175_out, and_176_out, and_177_out, and_178_out, and_179_out, and_180_out, and_181_out, and_182_out, and_183_out, and_184_out, and_185_out, and_186_out, and_187_out);
  or or_8 (or_8_out, and_1_out, and_2_out, and_3_out, and_4_out, and_5_out, and_6_out, and_7_out, and_8_out, and_9_out, and_10_out, and_11_out, and_12_out, and_13_out, and_14_out, and_15_out, and_16_out, and_17_out, and_18_out, and_19_out, and_20_out, and_21_out, and_22_out, and_23_out, and_24_out, and_25_out, and_26_out, and_27_out, and_28_out, and_29_out, and_30_out);
  or or_9 (h0, or_8_out, or_10_out, or_11_out);
  or or_10 (or_10_out, and_31_out, and_32_out, and_33_out, and_34_out, and_35_out, and_36_out, and_37_out, and_38_out, and_39_out, and_40_out, and_41_out, and_42_out, and_43_out, and_44_out, and_45_out, and_46_out, and_47_out, and_48_out, and_49_out, and_50_out, and_51_out, and_52_out, and_53_out, and_54_out, and_55_out, and_56_out, and_57_out, and_58_out, and_59_out, and_60_out);
  or or_11 (or_11_out, and_61_out, and_62_out, and_63_out, and_64_out, and_65_out, and_66_out, and_67_out, and_68_out, and_69_out, and_70_out, and_71_out, and_72_out, and_73_out, and_74_out, and_75_out, and_76_out, and_77_out, and_78_out, and_79_out, and_80_out, and_81_out, and_82_out, and_83_out, and_84_out, and_85_out, and_86_out, and_87_out, and_88_out, and_89_out, and_90_out);
  or or_12 (h1, or_4_out, or_5_out, or_6_out, or_7_out);
endmodule

module decalhorraire (
  input  rst,
  input  Button,
  output [5:0] hour1,
  output [5:0] hour0,
  output [5:0] min1,
  output [5:0] min0,
  output [5:0] sec1,
  output [5:0] sec0,
  output [4:0] hour_shift
);

  wire d_ff_1_q, d_ff_2_q, d_ff_3_q, d_ff_4_q;
  wire [5:0] selcomp_1_output_bus_1, selcomp_2_output_bus_1, selcomp_3_output_bus_1, selcomp_4_output_bus_1,
       selcomp_5_output_bus_1, selcomp_6_output_bus_1, selcomp_7_output_bus_1, selcomp_8_output_bus_1,
       selcomp_9_output_bus_1, selcomp_10_output_bus_1, selcomp_11_output_bus_1, selcomp_12_output_bus_1;

  D_Flip_Flop d_ff_1 (.D(d_ff_4_q), .clk(Button), .Q(d_ff_1_q), .preset(rst));  // open: Qn, reset
  D_Flip_Flop d_ff_2 (.D(d_ff_1_q), .clk(Button), .Q(d_ff_2_q), .reset(rst));  // open: Qn, preset
  D_Flip_Flop d_ff_3 (.D(d_ff_2_q), .clk(Button), .Q(d_ff_3_q), .reset(rst));  // open: Qn, preset
  D_Flip_Flop d_ff_4 (.D(d_ff_3_q), .clk(Button), .Q(d_ff_4_q), .reset(rst));  // open: Qn, preset
  selcomp selcomp_1 (
    .en(d_ff_1_q), .Input_1(1'b1), .Input_2(1'b0), .Input_3(1'b0), .Input_4(1'b0), .Input_5(1'b1),
    .Input_6(1'b0), .Output_bus_1(selcomp_1_output_bus_1));
  selcomp selcomp_2 (
    .en(d_ff_1_q), .Input_1(1'b1), .Input_2(1'b1), .Input_3(1'b1), .Input_4(1'b0), .Input_5(1'b1),
    .Input_6(1'b0), .Output_bus_1(selcomp_2_output_bus_1));
  selcomp selcomp_3 (
    .en(d_ff_1_q), .Input_1(1'b0), .Input_2(1'b1), .Input_3(1'b1), .Input_4(1'b1), .Input_5(1'b1),
    .Input_6(1'b0), .Output_bus_1(selcomp_3_output_bus_1));
  selcomp selcomp_4 (
    .en(d_ff_2_q), .Input_1(1'b0), .Input_2(1'b1), .Input_3(1'b0), .Input_4(1'b1), .Input_5(1'b1),
    .Input_6(1'b0), .Output_bus_1(selcomp_4_output_bus_1));
  selcomp selcomp_5 (
    .en(d_ff_2_q), .Input_1(1'b0), .Input_2(1'b0), .Input_3(1'b1), .Input_4(1'b1), .Input_5(1'b1),
    .Input_6(1'b0), .Output_bus_1(selcomp_5_output_bus_1));
  selcomp selcomp_6 (
    .en(d_ff_2_q), .Input_1(1'b1), .Input_2(1'b0), .Input_3(1'b1), .Input_4(1'b1), .Input_5(1'b1),
    .Input_6(1'b0), .Output_bus_1(selcomp_6_output_bus_1));
  selcomp selcomp_7 (
    .en(d_ff_3_q), .Input_1(1'b1), .Input_2(1'b1), .Input_3(1'b1), .Input_4(1'b0), .Input_5(1'b1),
    .Input_6(1'b0), .Output_bus_1(selcomp_7_output_bus_1));
  selcomp selcomp_8 (
    .en(d_ff_3_q), .Input_1(1'b1), .Input_2(1'b0), .Input_3(1'b1), .Input_4(1'b1), .Input_5(1'b1),
    .Input_6(1'b0), .Output_bus_1(selcomp_8_output_bus_1));
  selcomp selcomp_9 (
    .en(d_ff_3_q), .Input_1(1'b1), .Input_2(1'b0), .Input_3(1'b1), .Input_4(1'b1), .Input_5(1'b0),
    .Input_6(1'b0), .Output_bus_1(selcomp_9_output_bus_1));
  selcomp selcomp_10 (
    .en(d_ff_4_q), .Input_1(1'b0), .Input_2(1'b0), .Input_3(1'b0), .Input_4(1'b1), .Input_5(1'b1),
    .Input_6(1'b0), .Output_bus_1(selcomp_10_output_bus_1));
  selcomp selcomp_11 (
    .en(d_ff_4_q), .Input_1(1'b1), .Input_2(1'b0), .Input_3(1'b0), .Input_4(1'b0), .Input_5(1'b0),
    .Input_6(1'b1), .Output_bus_1(selcomp_11_output_bus_1));
  selcomp selcomp_12 (
    .en(d_ff_4_q), .Input_1(1'b1), .Input_2(1'b0), .Input_3(1'b1), .Input_4(1'b1), .Input_5(1'b0),
    .Input_6(1'b0), .Output_bus_1(selcomp_12_output_bus_1));
  shift shift_1 (
    .c1(d_ff_4_q), .c2(d_ff_3_q), .c3(d_ff_2_q), .c4(d_ff_1_q), .b0(hour_shift[0]), .b1(hour_shift[1]),
    .b2(hour_shift[2]), .b3(hour_shift[3]), .b4(hour_shift[4]));
  tens tens_1 (
    .Input_1(1'b0), .Input_2(hour_shift[4]), .Input_3(hour_shift[3]), .Input_4(hour_shift[2]),
    .Input_5(hour_shift[1]), .Input_6(hour_shift[0]), .Output_1(sec1[5]), .Output_2(sec1[4]),
    .Output_3(sec1[3]), .Output_4(sec1[2]), .Output_5(sec1[1]), .Output_6(sec1[0]));
  ones ones_1 (
    .Input_1(1'b0), .Input_2(hour_shift[4]), .Input_3(hour_shift[3]), .Input_4(hour_shift[2]),
    .Input_5(hour_shift[1]), .Input_6(hour_shift[0]), .Output_1(sec0[5]), .Output_2(sec0[4]),
    .Output_3(sec0[3]), .Output_4(sec0[2]), .Output_5(sec0[1]), .Output_6(sec0[0]));
  assign hour1 = selcomp_1_output_bus_1 | selcomp_4_output_bus_1 | selcomp_7_output_bus_1 | selcomp_10_output_bus_1;  // OR_Gate or_1, 6 bits wide
  assign hour0 = selcomp_2_output_bus_1 | selcomp_5_output_bus_1 | selcomp_8_output_bus_1 | selcomp_11_output_bus_1;  // OR_Gate or_2, 6 bits wide
  assign min1 = selcomp_3_output_bus_1 | selcomp_6_output_bus_1 | selcomp_9_output_bus_1 | selcomp_12_output_bus_1;  // OR_Gate or_3, 6 bits wide

  assign min0 = 6'b001010;

  // Notes on the sheet:
  //   londre
  //   moscou
  //   ldn
  //   mscu
  //   new-york
  //   nyk
  //   paris
  //   moscou
  //   MSC
  //   Greenwitch
  //   GRW
  //   prs
  //   newyork
  //   NYC
endmodule

module selcomp (
  input  en,
  input  Input_1,
  input  Input_2,
  input  Input_3,
  input  Input_4,
  input  Input_5,
  input  Input_6,
  output [5:0] Output_bus_1
);

  and and_1 (Output_bus_1[0], en, Input_1);
  and and_2 (Output_bus_1[1], en, Input_2);
  and and_3 (Output_bus_1[2], en, Input_3);
  and and_4 (Output_bus_1[3], en, Input_4);
  and and_5 (Output_bus_1[4], en, Input_5);
  and and_6 (Output_bus_1[5], en, Input_6);
endmodule

module shift (
  input  c1,
  input  c2,
  input  c3,
  input  c4,
  output b0,
  output b1,
  output b2,
  output b3,
  output b4
);

  wire not_2_out, not_3_out;

  not not_1 (b0, c4);
  not not_2 (not_2_out, c3);
  not not_3 (not_3_out, c4);
  and and_1 (b1, not_2_out, not_3_out);

  assign b2 = 1'b0;
  assign b3 = 1'b0;
  assign b4 = c1;
endmodule

module smartbutton (
  input  button,
  input  clk,
  output fall,
  output long,
  output Tlong
);

  wire and_1_out, and_2_out, and_3_out, and_4_out, and_5_out, and_6_out, and_7_out, and_8_out, and_9_out,
       and_10_out, and_11_out, and_12_out, and_13_out, d_ff_1_q, d_ff_2_q, t_ff_1_q, t_ff_2_q, t_ff_3_q,
       t_ff_4_q, t_ff_5_q, t_ff_6_q, t_ff_7_q, t_ff_8_q, t_ff_9_q, t_ff_10_q, t_ff_11_q, t_ff_12_q;

  T_Flip_Flop t_ff_1 (.T(button), .clk(clk), .Q(t_ff_1_q), .reset(and_2_out));  // open: Qn, preset
  D_Flip_Flop d_ff_1 (.D(button), .clk(clk), .Q(d_ff_1_q));  // open: Qn, preset, reset
  and and_1 (and_1_out, button, t_ff_1_q);
  D_Flip_Flop d_ff_2 (.D(d_ff_1_q), .clk(clk), .Q(d_ff_2_q));  // open: Qn, preset, reset
  T_Flip_Flop t_ff_2 (.T(and_1_out), .clk(clk), .Q(t_ff_2_q), .reset(and_2_out));  // open: Qn, preset
  and and_2 (and_2_out, ~d_ff_1_q, d_ff_2_q);  // AND_Gate
  T_Flip_Flop t_ff_3 (.T(and_3_out), .clk(clk), .Q(t_ff_3_q), .reset(and_2_out));  // open: Qn, preset
  and and_3 (and_3_out, and_1_out, t_ff_2_q);
  T_Flip_Flop t_ff_4 (.T(and_4_out), .clk(clk), .Q(t_ff_4_q), .reset(and_2_out));  // open: Qn, preset
  and and_4 (and_4_out, and_3_out, t_ff_3_q);
  T_Flip_Flop t_ff_5 (.T(and_5_out), .clk(clk), .Q(t_ff_5_q), .reset(and_2_out));  // open: Qn, preset
  and and_5 (and_5_out, and_4_out, t_ff_4_q);
  and and_6 (and_6_out, and_5_out, t_ff_5_q);
  T_Flip_Flop t_ff_6 (.T(and_6_out), .clk(clk), .Q(t_ff_6_q), .reset(and_2_out));  // open: Qn, preset
  T_Flip_Flop t_ff_7 (.T(and_7_out), .clk(clk), .Q(t_ff_7_q), .reset(and_2_out));  // open: Qn, preset
  and and_7 (and_7_out, and_6_out, t_ff_6_q);
  T_Flip_Flop t_ff_8 (.T(and_8_out), .clk(clk), .Q(t_ff_8_q), .reset(and_2_out));  // open: Qn, preset
  and and_8 (and_8_out, and_7_out, t_ff_7_q);
  T_Flip_Flop t_ff_9 (.T(and_9_out), .clk(clk), .Q(t_ff_9_q), .reset(and_2_out));  // open: Qn, preset
  and and_9 (and_9_out, and_8_out, t_ff_8_q);
  and and_10 (and_10_out, and_9_out, t_ff_9_q);
  T_Flip_Flop t_ff_10 (.T(and_10_out), .clk(clk), .Q(t_ff_10_q), .reset(and_2_out));  // open: Qn, preset
  T_Flip_Flop t_ff_11 (.T(and_11_out), .clk(clk), .Q(t_ff_11_q), .reset(and_2_out));  // open: Qn, preset
  and and_11 (and_11_out, and_10_out, t_ff_10_q);
  T_Flip_Flop t_ff_12 (.T(and_12_out), .clk(clk), .Q(t_ff_12_q), .reset(and_2_out));  // open: Qn, preset
  and and_12 (and_12_out, and_11_out, t_ff_11_q);
  T_Flip_Flop t_ff_13 (.T(and_13_out), .clk(clk), .Q(long), .reset(and_2_out));  // open: Qn, preset
  and and_13 (and_13_out, and_12_out, t_ff_12_q);
  and and_14 (fall, and_2_out, ~long);  // AND_Gate
endmodule

module ModHorloge (
  input  mrst,
  input  clk,
  input  LongA,
  input  ButtA,
  input  ButtB,
  input  [4:0] shift,
  output [5:0] s0,
  output [5:0] s1,
  output [5:0] m0,
  output [5:0] m1,
  output [5:0] h0,
  output [5:0] h1
);

  wire [4:0] Horloge_1_hours, rectifieurhorraire_1_h4;
  wire [5:0] Horloge_1_minutes, Horloge_1_seconds;
  wire [9:0] Horloge_1_ms;

  Horloge Horloge_1 (
    .MRST(mrst), .clk(clk), .longA(LongA), .FallA(ButtA), .FallB(ButtB), .ms(Horloge_1_ms),
    .Seconds(Horloge_1_seconds), .Minutes(Horloge_1_minutes), .Hours(Horloge_1_hours));
  rectifieurhorraire rectifieurhorraire_1 (
    .bh0(Horloge_1_hours[4]), .bh1(Horloge_1_hours[3]), .bh2(Horloge_1_hours[2]), .bh3(Horloge_1_hours[1]),
    .bh4(Horloge_1_hours[0]), .sh0(shift[4]), .sh1(shift[3]), .sh2(shift[2]), .sh3(shift[1]), .sh4(shift[0]),
    .h0(rectifieurhorraire_1_h4[4]), .h1(rectifieurhorraire_1_h4[3]), .h2(rectifieurhorraire_1_h4[2]),
    .h3(rectifieurhorraire_1_h4[1]), .h4(rectifieurhorraire_1_h4[0]));
  ones ones_1 (
    .Input_1(Horloge_1_seconds[5]), .Input_2(Horloge_1_seconds[4]), .Input_3(Horloge_1_seconds[3]),
    .Input_4(Horloge_1_seconds[2]), .Input_5(Horloge_1_seconds[1]), .Input_6(Horloge_1_seconds[0]),
    .Output_1(s0[5]), .Output_2(s0[4]), .Output_3(s0[3]), .Output_4(s0[2]), .Output_5(s0[1]), .Output_6(s0[0]));
  tens tens_1 (
    .Input_1(Horloge_1_seconds[5]), .Input_2(Horloge_1_seconds[4]), .Input_3(Horloge_1_seconds[3]),
    .Input_4(Horloge_1_seconds[2]), .Input_5(Horloge_1_seconds[1]), .Input_6(Horloge_1_seconds[0]),
    .Output_1(s1[5]), .Output_2(s1[4]), .Output_3(s1[3]), .Output_4(s1[2]), .Output_5(s1[1]), .Output_6(s1[0]));
  ones ones_2 (
    .Input_1(Horloge_1_minutes[5]), .Input_2(Horloge_1_minutes[4]), .Input_3(Horloge_1_minutes[3]),
    .Input_4(Horloge_1_minutes[2]), .Input_5(Horloge_1_minutes[1]), .Input_6(Horloge_1_minutes[0]),
    .Output_1(m0[5]), .Output_2(m0[4]), .Output_3(m0[3]), .Output_4(m0[2]), .Output_5(m0[1]), .Output_6(m0[0]));
  tens tens_2 (
    .Input_1(Horloge_1_minutes[5]), .Input_2(Horloge_1_minutes[4]), .Input_3(Horloge_1_minutes[3]),
    .Input_4(Horloge_1_minutes[2]), .Input_5(Horloge_1_minutes[1]), .Input_6(Horloge_1_minutes[0]),
    .Output_1(m1[5]), .Output_2(m1[4]), .Output_3(m1[3]), .Output_4(m1[2]), .Output_5(m1[1]), .Output_6(m1[0]));
  ones ones_3 (
    .Input_1(1'b0), .Input_2(rectifieurhorraire_1_h4[4]), .Input_3(rectifieurhorraire_1_h4[3]),
    .Input_4(rectifieurhorraire_1_h4[2]), .Input_5(rectifieurhorraire_1_h4[1]),
    .Input_6(rectifieurhorraire_1_h4[0]), .Output_1(h0[5]), .Output_2(h0[4]), .Output_3(h0[3]),
    .Output_4(h0[2]), .Output_5(h0[1]), .Output_6(h0[0]));
  tens tens_3 (
    .Input_1(1'b0), .Input_2(rectifieurhorraire_1_h4[4]), .Input_3(rectifieurhorraire_1_h4[3]),
    .Input_4(rectifieurhorraire_1_h4[2]), .Input_5(rectifieurhorraire_1_h4[1]),
    .Input_6(rectifieurhorraire_1_h4[0]), .Output_1(h1[5]), .Output_2(h1[4]), .Output_3(h1[3]),
    .Output_4(h1[2]), .Output_5(h1[1]), .Output_6(h1[0]));
endmodule

module changehour (
  input  rst,
  input  buttonA,
  input  buttonB,
  output [5:0] m0,
  output [5:0] m1,
  output [5:0] h0,
  output [5:0] h1,
  output [5:0] min,
  output [5:0] hour
);

  wire and_1_out, and_2_out, and_3_out, and_4_out, d_ff_1_q, d_ff_1_qn, d_ff_2_q, d_ff_3_q, d_ff_4_q,
       d_ff_5_q, d_ff_6_q, d_ff_7_q, d_ff_8_q, d_ff_9_q, d_ff_10_q, d_ff_11_q, or_1_out, or_2_out;

  D_Flip_Flop d_ff_1 (.D(d_ff_1_qn), .clk(buttonA), .Q(d_ff_1_q), .Qn(d_ff_1_qn), .preset(rst));  // open: reset
  and and_1 (and_1_out, d_ff_1_q, buttonB);
  and and_2 (and_2_out, d_ff_1_qn, buttonB);
  or or_1 (or_1_out, rst, and_3_out);
  or or_2 (or_2_out, rst, and_4_out);
  D_Flip_Flop d_ff_2 (.D(min[0]), .clk(and_1_out), .Q(d_ff_2_q), .Qn(min[0]), .preset(or_1_out));  // open: reset
  and and_3 (and_3_out, ~min[0], ~min[1], min[2], min[3], min[4], min[5]);  // AND_Gate
  D_Flip_Flop d_ff_3 (.D(hour[0]), .clk(and_2_out), .Q(d_ff_3_q), .Qn(hour[0]), .preset(or_2_out));  // open: reset
  and and_4 (and_4_out, ~hour[0], ~hour[1], ~hour[2], hour[3], hour[4]);  // AND_Gate
  D_Flip_Flop d_ff_4 (.D(min[1]), .clk(d_ff_2_q), .Q(d_ff_4_q), .Qn(min[1]), .preset(or_1_out));  // open: reset
  D_Flip_Flop d_ff_5 (.D(hour[1]), .clk(d_ff_3_q), .Q(d_ff_5_q), .Qn(hour[1]), .preset(or_2_out));  // open: reset
  D_Flip_Flop d_ff_6 (.D(min[2]), .clk(d_ff_4_q), .Q(d_ff_6_q), .Qn(min[2]), .preset(or_1_out));  // open: reset
  D_Flip_Flop d_ff_7 (.D(hour[2]), .clk(d_ff_5_q), .Q(d_ff_7_q), .Qn(hour[2]), .preset(or_2_out));  // open: reset
  D_Flip_Flop d_ff_8 (.D(min[3]), .clk(d_ff_6_q), .Q(d_ff_8_q), .Qn(min[3]), .preset(or_1_out));  // open: reset
  D_Flip_Flop d_ff_9 (.D(hour[3]), .clk(d_ff_7_q), .Q(d_ff_9_q), .Qn(hour[3]), .preset(or_2_out));  // open: reset
  D_Flip_Flop d_ff_10 (.D(min[4]), .clk(d_ff_8_q), .Q(d_ff_10_q), .Qn(min[4]), .preset(or_1_out));  // open: reset
  D_Flip_Flop d_ff_11 (.D(hour[4]), .clk(d_ff_9_q), .Q(d_ff_11_q), .Qn(hour[4]), .preset(or_2_out));  // open: reset
  D_Flip_Flop d_ff_12 (.D(min[5]), .clk(d_ff_10_q), .Qn(min[5]), .preset(or_1_out));  // open: Q, reset
  ones ones_1 (
    .Input_1(min[5]), .Input_2(min[4]), .Input_3(min[3]), .Input_4(min[2]), .Input_5(min[1]),
    .Input_6(min[0]), .Output_1(m0[5]), .Output_2(m0[4]), .Output_3(m0[3]), .Output_4(m0[2]),
    .Output_5(m0[1]), .Output_6(m0[0]));
  tens tens_1 (
    .Input_1(min[5]), .Input_2(min[4]), .Input_3(min[3]), .Input_4(min[2]), .Input_5(min[1]),
    .Input_6(min[0]), .Output_1(m1[5]), .Output_2(m1[4]), .Output_3(m1[3]), .Output_4(m1[2]),
    .Output_5(m1[1]), .Output_6(m1[0]));
  ones ones_2 (
    .Input_1(1'b0), .Input_2(hour[4]), .Input_3(hour[3]), .Input_4(hour[2]), .Input_5(hour[1]),
    .Input_6(hour[0]), .Output_1(h0[5]), .Output_2(h0[4]), .Output_3(h0[3]), .Output_4(h0[2]),
    .Output_5(h0[1]), .Output_6(h0[0]));
  tens tens_2 (
    .Input_1(1'b0), .Input_2(hour[4]), .Input_3(hour[3]), .Input_4(hour[2]), .Input_5(hour[1]),
    .Input_6(hour[0]), .Output_1(h1[5]), .Output_2(h1[4]), .Output_3(h1[3]), .Output_4(h1[2]),
    .Output_5(h1[1]), .Output_6(h1[0]));

  assign hour[5] = 1'b0;
endmodule

module Nhor (
  input  MSRT,
  input  clk,
  input  choice,
  input  button,
  input  load,
  output [5:0] sec,
  output [5:0] min,
  output [4:0] hour
);

  wire and_1_out, and_2_out, and_3_out, and_4_out, and_5_out, and_6_out, and_7_out, and_8_out, and_9_out,
       and_10_out, and_11_out, and_12_out, and_13_out, and_14_out, and_15_out, and_16_out, and_17_out,
       and_18_out, and_19_out, and_20_out, and_21_out, and_22_out, and_23_out, and_24_out, and_25_out,
       and_26_out, and_27_out, and_28_out, and_29_out, and_30_out, and_31_out, and_32_out, and_33_out,
       and_34_out, and_35_out, and_36_out, and_37_out, and_38_out, and_39_out, and_40_out, and_41_out,
       and_42_out, and_43_out, and_44_out, and_45_out, and_46_out, and_47_out, and_48_out, and_49_out,
       and_50_out, and_51_out, and_52_out, and_53_out, d_ff_1_q, d_ff_2_q, d_ff_3_q, d_ff_4_q, d_ff_5_q,
       d_ff_6_q, d_ff_7_q, d_ff_8_q, d_ff_9_q, d_ff_10_q, d_ff_12_q, d_ff_12_qn, d_ff_13_q, d_ff_13_qn,
       d_ff_14_q, d_ff_15_q, d_ff_16_q, d_ff_17_q, d_ff_17_qn, d_ff_18_q, d_ff_18_qn, d_ff_19_q, d_ff_20_q,
       d_ff_21_q, d_ff_22_q, d_ff_22_qn, d_ff_23_q, d_ff_23_qn, d_ff_24_q, d_ff_25_q, d_ff_26_q, d_ff_27_q,
       d_ff_27_qn, d_ff_28_q, d_ff_29_q, d_ff_30_q, d_ff_31_q, d_ff_31_qn, d_ff_32_q, d_ff_33_q, d_ff_34_q,
       d_ff_35_q, d_ff_35_qn, d_ff_38_q, d_ff_38_qn, d_ff_39_q, d_ff_39_qn, d_ff_40_q, d_ff_40_qn,
       d_ff_41_qn, or_1_out, or_2_out, or_3_out, or_4_out, or_5_out, or_6_out, or_7_out, or_8_out, or_9_out,
       or_10_out, or_11_out, or_12_out, or_13_out, or_14_out, or_15_out, or_16_out, or_17_out, undriven,
       undriven_2;
  wire [4:0] d_ff_2_qn;
  wire [5:0] d_ff_1_qn;

  and and_1 (and_1_out, undriven, button);
  and and_2 (and_2_out, undriven_2, button);
  or or_1 (or_1_out, MSRT, and_3_out);
  D_Flip_Flop d_ff_1 (
    .D(d_ff_1_qn[0]), .clk(and_1_out), .Q(d_ff_1_q), .Qn(d_ff_1_qn[0]), .preset(or_1_out));  // open: reset
  or or_2 (or_2_out, MSRT, and_4_out);
  D_Flip_Flop d_ff_2 (
    .D(d_ff_2_qn[0]), .clk(and_2_out), .Q(d_ff_2_q), .Qn(d_ff_2_qn[0]), .preset(or_2_out));  // open: reset
  D_Flip_Flop d_ff_3 (
    .D(d_ff_1_qn[1]), .clk(d_ff_1_q), .Q(d_ff_3_q), .Qn(d_ff_1_qn[1]), .preset(or_1_out));  // open: reset
  and and_3 (and_3_out, ~d_ff_1_qn[0], ~d_ff_1_qn[1], d_ff_1_qn[2], d_ff_1_qn[3], d_ff_1_qn[4], d_ff_1_qn[5]);  // AND_Gate
  D_Flip_Flop d_ff_4 (
    .D(d_ff_2_qn[1]), .clk(d_ff_2_q), .Q(d_ff_4_q), .Qn(d_ff_2_qn[1]), .preset(or_2_out));  // open: reset
  and and_4 (and_4_out, ~d_ff_2_qn[0], ~d_ff_2_qn[1], ~d_ff_2_qn[2], d_ff_2_qn[3], d_ff_2_qn[4]);  // AND_Gate
  D_Flip_Flop d_ff_5 (
    .D(d_ff_1_qn[2]), .clk(d_ff_3_q), .Q(d_ff_5_q), .Qn(d_ff_1_qn[2]), .preset(or_1_out));  // open: reset
  D_Flip_Flop d_ff_6 (
    .D(d_ff_2_qn[2]), .clk(d_ff_4_q), .Q(d_ff_6_q), .Qn(d_ff_2_qn[2]), .preset(or_2_out));  // open: reset
  D_Flip_Flop d_ff_7 (
    .D(d_ff_1_qn[3]), .clk(d_ff_5_q), .Q(d_ff_7_q), .Qn(d_ff_1_qn[3]), .preset(or_1_out));  // open: reset
  D_Flip_Flop d_ff_8 (
    .D(d_ff_2_qn[3]), .clk(d_ff_6_q), .Q(d_ff_8_q), .Qn(d_ff_2_qn[3]), .preset(or_2_out));  // open: reset
  and and_5 (and_5_out, and_7_out, load);
  and and_6 (and_6_out, and_8_out, load);
  and and_7 (and_7_out, 1'b1, ~d_ff_1_qn[0]);  // AND_Gate
  and and_8 (and_8_out, 1'b1, d_ff_1_qn[0]);
  and and_9 (and_9_out, and_12_out, load);
  and and_10 (and_10_out, and_11_out, load);
  and and_11 (and_11_out, 1'b1, d_ff_2_qn[0]);
  and and_12 (and_12_out, 1'b1, ~d_ff_2_qn[0]);  // AND_Gate
  D_Flip_Flop d_ff_9 (
    .D(d_ff_1_qn[4]), .clk(d_ff_7_q), .Q(d_ff_9_q), .Qn(d_ff_1_qn[4]), .preset(or_1_out));  // open: reset
  D_Flip_Flop d_ff_10 (
    .D(d_ff_2_qn[4]), .clk(d_ff_8_q), .Q(d_ff_10_q), .Qn(d_ff_2_qn[4]), .preset(or_2_out));  // open: reset
  and and_13 (and_13_out, and_16_out, load);
  and and_14 (and_14_out, and_15_out, load);
  and and_15 (and_15_out, 1'b1, d_ff_1_qn[1]);
  and and_16 (and_16_out, 1'b1, ~d_ff_1_qn[1]);  // AND_Gate
  and and_17 (and_17_out, 1'b1, ~d_ff_1_qn[2]);  // AND_Gate
  and and_18 (and_18_out, and_22_out, load);
  and and_19 (and_19_out, and_21_out, load);
  and and_20 (and_20_out, and_23_out, load);
  and and_21 (and_21_out, 1'b1, ~d_ff_2_qn[2]);  // AND_Gate
  and and_22 (and_22_out, 1'b1, ~d_ff_2_qn[1]);  // AND_Gate
  and and_23 (and_23_out, 1'b1, d_ff_2_qn[1]);
  D_Flip_Flop d_ff_11 (.D(d_ff_1_qn[5]), .clk(d_ff_9_q), .Qn(d_ff_1_qn[5]), .preset(or_1_out));  // open: Q, reset
  and and_24 (and_24_out, and_17_out, load);
  and and_25 (and_25_out, and_28_out, load);
  and and_26 (and_26_out, and_27_out, load);
  and and_27 (and_27_out, 1'b1, d_ff_1_qn[2]);
  and and_28 (and_28_out, 1'b1, ~d_ff_1_qn[3]);  // AND_Gate
  and and_29 (and_29_out, and_31_out, load);
  and and_30 (and_30_out, and_33_out, load);
  and and_31 (and_31_out, 1'b1, ~d_ff_2_qn[3]);  // AND_Gate
  and and_32 (and_32_out, 1'b1, d_ff_2_qn[3]);
  and and_33 (and_33_out, 1'b1, d_ff_2_qn[2]);
  and and_34 (and_34_out, and_38_out, load);
  and and_35 (and_35_out, and_39_out, load);
  and and_36 (and_36_out, and_37_out, load);
  and and_37 (and_37_out, 1'b1, d_ff_1_qn[4]);
  and and_38 (and_38_out, 1'b1, ~d_ff_1_qn[4]);  // AND_Gate
  and and_39 (and_39_out, 1'b1, d_ff_1_qn[3]);
  and and_40 (and_40_out, and_44_out, load);
  and and_41 (and_41_out, and_32_out, load);
  and and_42 (and_42_out, and_43_out, load);
  and and_43 (and_43_out, 1'b1, d_ff_2_qn[4]);
  and and_44 (and_44_out, 1'b1, ~d_ff_2_qn[4]);  // AND_Gate
  and and_45 (and_45_out, and_48_out, load);
  and and_46 (and_46_out, and_47_out, load);
  and and_47 (and_47_out, 1'b1, d_ff_1_qn[5]);
  and and_48 (and_48_out, 1'b1, ~d_ff_1_qn[5]);  // AND_Gate
  or or_3 (or_3_out, MSRT, and_50_out);
  or or_4 (or_4_out, MSRT, and_51_out);
  or or_5 (or_5_out, MSRT, and_52_out);
  or or_6 (or_6_out, MSRT, and_49_out);
  and and_49 (and_49_out, ~hour[0], ~hour[1], ~hour[2], hour[3], hour[4]);  // AND_Gate
  D_Flip_Flop d_ff_12 (.D(d_ff_12_qn), .clk(clk), .Q(d_ff_12_q), .Qn(d_ff_12_qn), .preset(MSRT));  // open: reset
  D_Flip_Flop d_ff_13 (
    .D(d_ff_13_qn), .clk(d_ff_22_q), .Q(d_ff_13_q), .Qn(d_ff_13_qn), .preset(or_3_out));  // open: reset
  and and_50 (and_50_out, d_ff_13_qn, ~d_ff_18_qn, ~d_ff_23_qn, d_ff_27_qn, ~d_ff_31_qn, d_ff_35_qn, d_ff_38_qn, d_ff_39_qn, d_ff_40_qn, d_ff_41_qn);  // AND_Gate
  D_Flip_Flop d_ff_14 (.D(sec[0]), .clk(and_53_out), .Q(d_ff_14_q), .Qn(sec[0]), .preset(or_4_out));  // open: reset
  and and_51 (and_51_out, ~sec[0], ~sec[1], sec[2], sec[3], sec[4], sec[5]);  // AND_Gate
  or or_7 (or_7_out, or_5_out, and_5_out);
  D_Flip_Flop d_ff_15 (.D(min[0]), .clk(and_51_out), .Q(d_ff_15_q), .Qn(min[0]), .preset(or_7_out), .reset(and_6_out));
  and and_52 (and_52_out, ~min[0], ~min[1], min[2], min[3], min[4], min[5]);  // AND_Gate
  or or_8 (or_8_out, or_6_out, and_9_out);
  D_Flip_Flop d_ff_16 (
    .D(hour[0]), .clk(and_52_out), .Q(d_ff_16_q), .Qn(hour[0]), .preset(or_8_out), .reset(and_10_out));
  D_Flip_Flop d_ff_17 (.D(d_ff_17_qn), .clk(d_ff_12_q), .Q(d_ff_17_q), .Qn(d_ff_17_qn), .preset(MSRT));  // open: reset
  D_Flip_Flop d_ff_18 (
    .D(d_ff_18_qn), .clk(d_ff_13_q), .Q(d_ff_18_q), .Qn(d_ff_18_qn), .preset(or_3_out));  // open: reset
  D_Flip_Flop d_ff_19 (.D(sec[1]), .clk(d_ff_14_q), .Q(d_ff_19_q), .Qn(sec[1]), .preset(or_4_out));  // open: reset
  or or_9 (or_9_out, or_5_out, and_13_out);
  D_Flip_Flop d_ff_20 (.D(min[1]), .clk(d_ff_15_q), .Q(d_ff_20_q), .Qn(min[1]), .preset(or_9_out), .reset(and_14_out));
  or or_10 (or_10_out, or_6_out, and_18_out);
  D_Flip_Flop d_ff_21 (
    .D(hour[1]), .clk(d_ff_16_q), .Q(d_ff_21_q), .Qn(hour[1]), .preset(or_10_out), .reset(and_20_out));
  D_Flip_Flop d_ff_22 (.D(d_ff_22_qn), .clk(d_ff_17_q), .Q(d_ff_22_q), .Qn(d_ff_22_qn), .preset(MSRT));  // open: reset
  D_Flip_Flop d_ff_23 (
    .D(d_ff_23_qn), .clk(d_ff_18_q), .Q(d_ff_23_q), .Qn(d_ff_23_qn), .preset(or_3_out));  // open: reset
  and and_53 (and_53_out, d_ff_13_qn, ~d_ff_18_qn, d_ff_23_qn, ~d_ff_27_qn, d_ff_31_qn, d_ff_35_qn, d_ff_38_qn, d_ff_39_qn, d_ff_40_qn);  // AND_Gate
  D_Flip_Flop d_ff_24 (.D(sec[2]), .clk(d_ff_19_q), .Q(d_ff_24_q), .Qn(sec[2]), .preset(or_4_out));  // open: reset
  or or_11 (or_11_out, or_5_out, and_24_out);
  D_Flip_Flop d_ff_25 (.D(min[2]), .clk(d_ff_20_q), .Q(d_ff_25_q), .Qn(min[2]), .preset(or_11_out), .reset(and_26_out));
  or or_12 (or_12_out, or_6_out, and_19_out);
  D_Flip_Flop d_ff_26 (
    .D(hour[2]), .clk(d_ff_21_q), .Q(d_ff_26_q), .Qn(hour[2]), .preset(or_12_out), .reset(and_30_out));
  D_Flip_Flop d_ff_27 (
    .D(d_ff_27_qn), .clk(d_ff_23_q), .Q(d_ff_27_q), .Qn(d_ff_27_qn), .preset(or_3_out));  // open: reset
  D_Flip_Flop d_ff_28 (.D(sec[3]), .clk(d_ff_24_q), .Q(d_ff_28_q), .Qn(sec[3]), .preset(or_4_out));  // open: reset
  or or_13 (or_13_out, or_5_out, and_25_out);
  D_Flip_Flop d_ff_29 (.D(min[3]), .clk(d_ff_25_q), .Q(d_ff_29_q), .Qn(min[3]), .preset(or_13_out), .reset(and_35_out));
  or or_14 (or_14_out, or_6_out, and_29_out);
  D_Flip_Flop d_ff_30 (
    .D(hour[3]), .clk(d_ff_26_q), .Q(d_ff_30_q), .Qn(hour[3]), .preset(or_14_out), .reset(and_41_out));
  D_Flip_Flop d_ff_31 (
    .D(d_ff_31_qn), .clk(d_ff_27_q), .Q(d_ff_31_q), .Qn(d_ff_31_qn), .preset(or_3_out));  // open: reset
  D_Flip_Flop d_ff_32 (.D(sec[4]), .clk(d_ff_28_q), .Q(d_ff_32_q), .Qn(sec[4]), .preset(or_4_out));  // open: reset
  or or_15 (or_15_out, or_5_out, and_34_out);
  D_Flip_Flop d_ff_33 (.D(min[4]), .clk(d_ff_29_q), .Q(d_ff_33_q), .Qn(min[4]), .preset(or_15_out), .reset(and_36_out));
  or or_16 (or_16_out, or_6_out, and_40_out);
  D_Flip_Flop d_ff_34 (
    .D(hour[4]), .clk(d_ff_30_q), .Q(d_ff_34_q), .Qn(hour[4]), .preset(or_16_out), .reset(and_42_out));
  D_Flip_Flop d_ff_35 (
    .D(d_ff_35_qn), .clk(d_ff_31_q), .Q(d_ff_35_q), .Qn(d_ff_35_qn), .preset(or_3_out));  // open: reset
  D_Flip_Flop d_ff_36 (.D(sec[5]), .clk(d_ff_32_q), .Qn(sec[5]), .preset(or_4_out));  // open: Q, reset
  or or_17 (or_17_out, or_5_out, and_45_out);
  D_Flip_Flop d_ff_37 (.D(min[5]), .clk(d_ff_33_q), .Qn(min[5]), .preset(or_17_out), .reset(and_46_out));  // open: Q
  D_Flip_Flop d_ff_38 (
    .D(d_ff_38_qn), .clk(d_ff_35_q), .Q(d_ff_38_q), .Qn(d_ff_38_qn), .preset(or_3_out));  // open: reset
  D_Flip_Flop d_ff_39 (
    .D(d_ff_39_qn), .clk(d_ff_38_q), .Q(d_ff_39_q), .Qn(d_ff_39_qn), .preset(or_3_out));  // open: reset
  D_Flip_Flop d_ff_40 (
    .D(d_ff_40_qn), .clk(d_ff_39_q), .Q(d_ff_40_q), .Qn(d_ff_40_qn), .preset(or_3_out));  // open: reset
  D_Flip_Flop d_ff_41 (.D(d_ff_41_qn), .clk(d_ff_40_q), .Qn(d_ff_41_qn), .preset(or_3_out));  // open: Q, reset
endmodule

module counter8bit (
  input  EN,
  input  clk,
  input  rst,
  input  WRITE,
  input  I7,
  input  I6,
  input  I5,
  input  I4,
  input  I3,
  input  I2,
  input  I1,
  input  I0,
  output OVRF,
  output O7,
  output O6,
  output O5,
  output O4,
  output O3,
  output O2,
  output O1,
  output O0
);

  wire and_1_out, and_2_out, and_3_out, and_4_out, and_5_out, and_6_out, and_7_out, and_8_out, and_9_out,
       and_10_out, and_11_out, and_12_out, and_13_out, and_14_out, and_15_out, and_16_out, and_17_out,
       and_18_out, and_19_out, and_20_out, and_21_out, and_22_out, and_24_out, not_1_out, not_2_out,
       not_3_out, not_4_out, not_5_out, not_6_out, not_7_out, not_8_out, or_1_out, or_2_out, or_3_out,
       or_4_out, or_5_out, or_6_out, or_7_out, or_8_out;

  T_Flip_Flop t_ff_1 (.T(EN), .clk(clk), .Q(O0), .reset(or_1_out), .preset(and_2_out));  // open: Qn
  and and_1 (and_1_out, EN, O0);
  or or_1 (or_1_out, rst, and_3_out);
  and and_2 (and_2_out, WRITE, I0);
  and and_3 (and_3_out, WRITE, not_1_out);
  not not_1 (not_1_out, I0);
  T_Flip_Flop t_ff_2 (.T(and_1_out), .clk(clk), .Q(O1), .reset(or_2_out), .preset(and_4_out));  // open: Qn
  or or_2 (or_2_out, rst, and_5_out);
  and and_4 (and_4_out, WRITE, I1);
  and and_5 (and_5_out, WRITE, not_2_out);
  not not_2 (not_2_out, I1);
  T_Flip_Flop t_ff_3 (.T(and_6_out), .clk(clk), .Q(O2), .reset(or_3_out), .preset(and_9_out));  // open: Qn
  and and_6 (and_6_out, and_1_out, O1);
  or or_3 (or_3_out, rst, and_7_out);
  and and_7 (and_7_out, WRITE, not_3_out);
  not not_3 (not_3_out, I2);
  T_Flip_Flop t_ff_4 (.T(and_8_out), .clk(clk), .Q(O3), .reset(or_4_out), .preset(and_12_out));  // open: Qn
  and and_8 (and_8_out, and_6_out, O2);
  or or_4 (or_4_out, rst, and_10_out);
  and and_9 (and_9_out, WRITE, I2);
  and and_10 (and_10_out, WRITE, not_4_out);
  T_Flip_Flop t_ff_5 (.T(and_11_out), .clk(clk), .Q(O4), .reset(or_5_out), .preset(and_15_out));  // open: Qn
  and and_11 (and_11_out, and_8_out, O3);
  and and_12 (and_12_out, WRITE, I3);
  not not_4 (not_4_out, I3);
  and and_13 (and_13_out, and_11_out, O4);
  or or_5 (or_5_out, rst, and_14_out);
  and and_14 (and_14_out, WRITE, not_5_out);
  and and_15 (and_15_out, WRITE, I4);
  not not_5 (not_5_out, I4);
  T_Flip_Flop t_ff_6 (.T(and_13_out), .clk(clk), .Q(O5), .reset(or_6_out), .preset(and_16_out));  // open: Qn
  or or_6 (or_6_out, rst, and_17_out);
  and and_16 (and_16_out, WRITE, I5);
  and and_17 (and_17_out, WRITE, not_6_out);
  not not_6 (not_6_out, I5);
  T_Flip_Flop t_ff_7 (.T(and_18_out), .clk(clk), .Q(O6), .reset(or_7_out), .preset(and_21_out));  // open: Qn
  and and_18 (and_18_out, and_13_out, O5);
  or or_7 (or_7_out, rst, and_19_out);
  and and_19 (and_19_out, WRITE, not_7_out);
  not not_7 (not_7_out, I6);
  T_Flip_Flop t_ff_8 (.T(and_20_out), .clk(clk), .Q(O7), .reset(or_8_out), .preset(and_24_out));  // open: Qn
  and and_20 (and_20_out, and_18_out, O6);
  or or_8 (or_8_out, rst, and_22_out);
  and and_21 (and_21_out, WRITE, I6);
  and and_22 (and_22_out, WRITE, not_8_out);
  and and_23 (OVRF, and_20_out, O7);
  and and_24 (and_24_out, WRITE, I7);
  not not_8 (not_8_out, I7);
endmodule
