// Logisim project sonneriedesesmorts.circ as structural Verilog: 8 circuits, main circuit main
module main (
  output Output_1,
  output terre
);

  wire and_1_out, and_2_out, and_3_out, and_4_out, and_5_out, and_6_out, and_7_out, and_8_out, and_9_out,
       Button_1_out, clock_1_out, counter_1_carry, d_ff_1_q, d_ff_2_q, d_ff_3_q, d_ff_4_q, d_ff_5_qn,
       demultiplexer_1_out0, demultiplexer_1_out1, demultiplexer_1_out2, demultiplexer_1_out3,
       demultiplexer_1_out4, demultiplexer_1_out5, demultiplexer_1_out6, demultiplexer_1_out7,
       demultiplexer_1_out8, demultiplexer_1_out9, demultiplexer_1_out10, demultiplexer_1_out11,
       demultiplexer_1_out12, demultiplexer_1_out13, demultiplexer_1_out14, demultiplexer_1_out15,
       dipswitch_1_sw1, not_1_out, nul_1_output_1, nul_2_output_1, nul_3_output_1, nul_4_output_1,
       nul_5_output_1, nul_6_output_1, nul_7_output_1, nul_8_output_1, or_1_out, or_2_out, or_3_out,
       unit_control_1_ending;
  wire [3:0] unit_control_1_ad_freq;
  wire [5:0] counter_1_q;

  DipSwitch dipswitch_1 (.sw1(dipswitch_1_sw1));  // open: sw2, sw3, sw4, sw5, sw6, sw7, sw8
  Button Button_1 (.out(Button_1_out));
  Clock clock_1 (.out(clock_1_out));
  Counter #(.width(6), .max('h3f)) counter_1 (
    .clr(or_3_out), .load(1'b0), .up(1'b1), .clk(clock_1_out), .carry(counter_1_carry),
    .Q({counter_1_q[0], counter_1_q[1], counter_1_q[2], counter_1_q[3], counter_1_q[4], counter_1_q[5]}));  // open: count, D
  D_Flip_Flop d_ff_1 (.D(Button_1_out), .clk(clock_1_out), .Q(d_ff_1_q));  // open: Qn, preset, reset
  D_Flip_Flop d_ff_2 (.D(d_ff_1_q), .clk(clock_1_out), .Q(d_ff_2_q));  // open: Qn, preset, reset
  and and_1 (and_1_out, d_ff_1_q, d_ff_2_q, d_ff_3_q, d_ff_4_q);
  D_Flip_Flop d_ff_3 (.D(d_ff_2_q), .clk(clock_1_out), .Q(d_ff_3_q));  // open: Qn, preset, reset
  D_Flip_Flop d_ff_4 (.D(d_ff_3_q), .clk(clock_1_out), .Q(d_ff_4_q));  // open: Qn, preset, reset
  not not_1 (not_1_out, unit_control_1_ending);
  Demultiplexer #(.select(4), .enable("false")) demultiplexer_1 (
    .out0(demultiplexer_1_out0), .out1(demultiplexer_1_out1), .out2(demultiplexer_1_out2),
    .out3(demultiplexer_1_out3), .out4(demultiplexer_1_out4), .out5(demultiplexer_1_out5),
    .out6(demultiplexer_1_out6), .out7(demultiplexer_1_out7), .out8(demultiplexer_1_out8),
    .out9(demultiplexer_1_out9), .out10(demultiplexer_1_out10), .out11(demultiplexer_1_out11),
    .out12(demultiplexer_1_out12), .out13(demultiplexer_1_out13), .out14(demultiplexer_1_out14),
    .out15(demultiplexer_1_out15), .in(not_1_out), .sel(unit_control_1_ad_freq));
  and and_2 (and_2_out, ~counter_1_q[5], ~counter_1_q[4], counter_1_q[3], ~counter_1_q[2], counter_1_q[1], counter_1_q[0], demultiplexer_1_out0);  // AND_Gate
  and and_3 (and_3_out, counter_1_q[5], counter_1_q[4], counter_1_q[3], ~counter_1_q[2], ~counter_1_q[1], counter_1_q[0], demultiplexer_1_out1);  // AND_Gate
  and and_4 (and_4_out, counter_1_q[5], ~counter_1_q[4], counter_1_q[3], ~counter_1_q[2], ~counter_1_q[1], counter_1_q[0], demultiplexer_1_out2);  // AND_Gate
  and and_5 (and_5_out, counter_1_q[5], ~counter_1_q[4], ~counter_1_q[3], ~counter_1_q[2], ~counter_1_q[1], counter_1_q[0], demultiplexer_1_out3);  // AND_Gate
  and and_6 (and_6_out, counter_1_q[5], counter_1_q[4], ~counter_1_q[3], ~counter_1_q[2], ~counter_1_q[1], counter_1_q[0], demultiplexer_1_out4);  // AND_Gate
  unit_control unit_control_1 (
    .EN(and_1_out), .RST_DIP(dipswitch_1_sw1), .ad_freq(unit_control_1_ad_freq),
    .ending(unit_control_1_ending));
  and and_7 (and_7_out, counter_1_q[5], ~counter_1_q[4], ~counter_1_q[3], counter_1_q[2], ~counter_1_q[1], counter_1_q[0], demultiplexer_1_out5);  // AND_Gate
  and and_8 (and_8_out, ~counter_1_q[5], counter_1_q[4], ~counter_1_q[3], counter_1_q[2], counter_1_q[1], ~counter_1_q[0], demultiplexer_1_out7);  // AND_Gate
  and and_9 (and_9_out, counter_1_q[5], ~counter_1_q[4], counter_1_q[3], counter_1_q[2], counter_1_q[1], ~counter_1_q[0], demultiplexer_1_out6);  // AND_Gate
  ending nul_1 (.Input_bus_1(counter_1_q), .Input_1(demultiplexer_1_out8), .Output_1(nul_1_output_1));
  ending nul_2 (.Input_bus_1(counter_1_q), .Input_1(demultiplexer_1_out9), .Output_1(nul_2_output_1));
  ending nul_3 (.Input_bus_1(counter_1_q), .Input_1(demultiplexer_1_out10), .Output_1(nul_3_output_1));
  ending nul_4 (.Input_bus_1(counter_1_q), .Input_1(demultiplexer_1_out11), .Output_1(nul_4_output_1));
  ending nul_5 (.Input_bus_1(counter_1_q), .Input_1(demultiplexer_1_out12), .Output_1(nul_5_output_1));
  ending nul_6 (.Input_bus_1(counter_1_q), .Input_1(demultiplexer_1_out13), .Output_1(nul_6_output_1));
  ending nul_7 (.Input_bus_1(counter_1_q), .Input_1(demultiplexer_1_out14), .Output_1(nul_7_output_1));
  ending nul_8 (.Input_bus_1(counter_1_q), .Input_1(demultiplexer_1_out15), .Output_1(nul_8_output_1));
  or or_1 (or_1_out, and_2_out, and_3_out, and_4_out, and_5_out, and_6_out, and_7_out, and_8_out, and_9_out);
  or or_2 (or_2_out, nul_1_output_1, nul_2_output_1, nul_3_output_1, nul_4_output_1, nul_5_output_1, nul_6_output_1, nul_7_output_1, nul_8_output_1);
  or or_3 (or_3_out, or_1_out, or_2_out);
  D_Flip_Flop d_ff_5 (.D(d_ff_5_qn), .clk(or_3_out), .Q(Output_1), .Qn(d_ff_5_qn));  // open: preset, reset

  assign terre = 1'b0;

  // Notes on the sheet:
  //   Debouncer
  //   B
  //   E
  //   F
  //   G
  //   F_s
  //   D_s
  //   B_2
  //   A_2
endmodule

module cmt (
  input  mute,
  input  set,
  input  reset,
  output [3:0] Output_bus_1
);

  wire and_1_out, and_2_out, and_3_out, and_4_out, t_ff_1_qn, t_ff_2_qn, t_ff_3_qn;

  and and_1 (and_1_out, 1'b0, mute);
  and and_2 (and_2_out, ~1'b0, mute);  // AND_Gate
  and and_3 (and_3_out, ~1'b0, mute);  // AND_Gate
  and and_4 (and_4_out, ~1'b0, mute);  // AND_Gate
  T_Flip_Flop t_ff_1 (.T(1'b1), .clk(set), .Q(Output_bus_1[0]), .Qn(t_ff_1_qn), .reset(reset), .preset(and_1_out));
  T_Flip_Flop t_ff_2 (
    .T(1'b1), .clk(t_ff_1_qn), .Q(Output_bus_1[1]), .Qn(t_ff_2_qn), .reset(reset), .preset(and_2_out));
  T_Flip_Flop t_ff_3 (
    .T(1'b1), .clk(t_ff_2_qn), .Q(Output_bus_1[2]), .Qn(t_ff_3_qn), .reset(reset), .preset(and_3_out));
  T_Flip_Flop t_ff_4 (.T(1'b1), .clk(t_ff_3_qn), .Q(Output_bus_1[3]), .reset(reset), .preset(and_4_out));  // open: Qn
endmodule

module partition (
  input  [3:0] cmt_part,
  output [3:0] freq,
  output [10:0] tempo
);

  Multiplexer #(.select(4), .width(4), .enable("false")) multiplexer_1 (
    .in0(4'b0000), .in1(4'b0001), .in2(4'b0011), .in3(4'b0010), .in4(4'b0001), .in5(4'b0111), .in6(4'b0110),
    .in7(4'b0100), .in8(4'b0001), .in9(4'b0011), .in10(4'b0010), .in11(4'b0101), .in12(4'b0010),
    .in13(4'b0000), .in14(4'b1110), .in15(4'b1110), .out(freq), .sel(cmt_part));
  Multiplexer #(.select(4), .width(11), .enable("false")) multiplexer_2 (
    .in0(11'h190), .in1(11'h258), .in2(11'hc8), .in3(11'h190), .in4(11'h320), .in5(11'h190), .in6(11'h3e8),
    .in7(11'h3e8), .in8(11'h258), .in9(11'hc8), .in10(11'h190), .in11(11'h320), .in12(11'h190),
    .in13(11'h3e8), .in14(11'h600), .in15(11'h400), .out(tempo), .sel(cmt_part));

  // Notes on the sheet:
  //   0.4
  //   0.6
  //   0.2
  //   0.8
  //   1
endmodule

module fin (
  input  [10:0] Input_bus_1,
  output Output_1
);

  and and_1 (Output_1, ~Input_bus_1[0], ~Input_bus_1[1], ~Input_bus_1[2], ~Input_bus_1[3], ~Input_bus_1[4], ~Input_bus_1[5], ~Input_bus_1[6], ~Input_bus_1[7], ~Input_bus_1[8], ~Input_bus_1[9], Input_bus_1[10]);  // AND_Gate
endmodule

module cmt_tempo (
  input  en_tmpo,
  input  [10:0] tempo_bis,
  input  clk_tempo,
  output set_tmpo
);

  wire t_ff_1_q, t_ff_1_qn, t_ff_2_q, t_ff_2_qn, t_ff_3_q, t_ff_3_qn, t_ff_4_q, t_ff_4_qn, t_ff_5_q,
       t_ff_5_qn, t_ff_6_q, t_ff_6_qn, t_ff_7_q, t_ff_7_qn, t_ff_8_q, t_ff_8_qn, t_ff_9_q, t_ff_9_qn,
       t_ff_10_q, t_ff_10_qn, t_ff_11_q, xnor_1_out, xnor_2_out, xnor_3_out, xnor_4_out, xnor_5_out,
       xnor_6_out, xnor_7_out, xnor_8_out, xnor_9_out, xnor_10_out, xnor_11_out;

  T_Flip_Flop t_ff_1 (.T(en_tmpo), .clk(clk_tempo), .Q(t_ff_1_q), .Qn(t_ff_1_qn), .reset(set_tmpo));  // open: preset
  T_Flip_Flop t_ff_2 (.T(en_tmpo), .clk(t_ff_1_qn), .Q(t_ff_2_q), .Qn(t_ff_2_qn), .reset(set_tmpo));  // open: preset
  T_Flip_Flop t_ff_3 (.T(en_tmpo), .clk(t_ff_2_qn), .Q(t_ff_3_q), .Qn(t_ff_3_qn), .reset(set_tmpo));  // open: preset
  T_Flip_Flop t_ff_4 (.T(en_tmpo), .clk(t_ff_3_qn), .Q(t_ff_4_q), .Qn(t_ff_4_qn), .reset(set_tmpo));  // open: preset
  T_Flip_Flop t_ff_5 (.T(en_tmpo), .clk(t_ff_4_qn), .Q(t_ff_5_q), .Qn(t_ff_5_qn), .reset(set_tmpo));  // open: preset
  T_Flip_Flop t_ff_6 (.T(en_tmpo), .clk(t_ff_5_qn), .Q(t_ff_6_q), .Qn(t_ff_6_qn), .reset(set_tmpo));  // open: preset
  T_Flip_Flop t_ff_7 (.T(en_tmpo), .clk(t_ff_6_qn), .Q(t_ff_7_q), .Qn(t_ff_7_qn), .reset(set_tmpo));  // open: preset
  T_Flip_Flop t_ff_8 (.T(en_tmpo), .clk(t_ff_7_qn), .Q(t_ff_8_q), .Qn(t_ff_8_qn), .reset(set_tmpo));  // open: preset
  T_Flip_Flop t_ff_9 (.T(en_tmpo), .clk(t_ff_8_qn), .Q(t_ff_9_q), .Qn(t_ff_9_qn), .reset(set_tmpo));  // open: preset
  T_Flip_Flop t_ff_10 (.T(en_tmpo), .clk(t_ff_9_qn), .Q(t_ff_10_q), .Qn(t_ff_10_qn), .reset(set_tmpo));  // open: preset
  T_Flip_Flop t_ff_11 (.T(en_tmpo), .clk(t_ff_10_qn), .Q(t_ff_11_q), .reset(set_tmpo));  // open: Qn, preset
  xnor xnor_1 (xnor_1_out, t_ff_11_q, tempo_bis[10]);
  xnor xnor_2 (xnor_2_out, t_ff_10_q, tempo_bis[9]);
  xnor xnor_3 (xnor_3_out, t_ff_9_q, tempo_bis[8]);
  xnor xnor_4 (xnor_4_out, t_ff_7_q, tempo_bis[6]);
  xnor xnor_5 (xnor_5_out, t_ff_8_q, tempo_bis[7]);
  xnor xnor_6 (xnor_6_out, t_ff_6_q, tempo_bis[5]);
  and and_1 (set_tmpo, xnor_1_out, xnor_2_out, xnor_3_out, xnor_5_out, xnor_4_out, xnor_6_out, xnor_7_out, xnor_9_out, xnor_8_out, xnor_10_out, xnor_11_out);
  xnor xnor_7 (xnor_7_out, t_ff_5_q, tempo_bis[4]);
  xnor xnor_8 (xnor_8_out, t_ff_3_q, tempo_bis[2]);
  xnor xnor_9 (xnor_9_out, t_ff_4_q, tempo_bis[3]);
  xnor xnor_10 (xnor_10_out, t_ff_2_q, tempo_bis[1]);
  xnor xnor_11 (xnor_11_out, t_ff_1_q, tempo_bis[0]);
endmodule

module ending (
  input  [5:0] Input_bus_1,
  input  Input_1,
  output Output_1
);

  and and_1 (Output_1, Input_bus_1[5], Input_bus_1[4], Input_bus_1[3], Input_bus_1[2], Input_bus_1[1], Input_bus_1[0], Input_1);
endmodule

module unit_control (
  input  EN,
  input  RST_DIP,
  output [3:0] ad_freq,
  output ending
);

  wire and_1_out, and_2_out, clock_1_out, cmt_tempo_1_set_tmpo, fin_1_output_1, not_1_out, not_2_out,
       or_1_out, or_3_out, to_mute_1_muting;
  wire [3:0] cmt_1_output_bus_1;
  wire [10:0] partition_1_tempo;

  Clock #(.highDuration(8), .lowDuration(8)) clock_1 (.out(clock_1_out));
  or or_1 (or_1_out, EN, fin_1_output_1);
  not not_1 (not_1_out, RST_DIP);
  and and_1 (and_1_out, not_1_out, or_1_out);
  not not_2 (not_2_out, fin_1_output_1);
  cmt_tempo cmt_tempo_1 (
    .en_tmpo(not_2_out), .tempo_bis(partition_1_tempo), .clk_tempo(clock_1_out),
    .set_tmpo(cmt_tempo_1_set_tmpo));
  or or_2 (ending, RST_DIP, fin_1_output_1);
  cmt cmt_1 (.mute(RST_DIP), .set(and_2_out), .reset(and_1_out), .Output_bus_1(cmt_1_output_bus_1));
  and and_2 (and_2_out, cmt_tempo_1_set_tmpo, ~or_3_out);  // AND_Gate
  or or_3 (or_3_out, to_mute_1_muting, fin_1_output_1);
  fin fin_1 (.Input_bus_1(partition_1_tempo), .Output_1(fin_1_output_1));
  to_mute to_mute_1 (.tempo(partition_1_tempo), .muting(to_mute_1_muting));
  partition partition_1 (.cmt_part(cmt_1_output_bus_1), .freq(ad_freq), .tempo(partition_1_tempo));
endmodule

module to_mute (
  input  [10:0] tempo,
  output muting
);

  and and_1 (muting, ~tempo[0], ~tempo[1], ~tempo[2], ~tempo[3], ~tempo[4], ~tempo[5], ~tempo[6], ~tempo[7], ~tempo[8], tempo[9], tempo[10]);  // AND_Gate
endmodule
